// Digital circuit cpu-32 test.dig as structural Verilog
module cpu_32_test (
  input  C,
  input  bus_e,
  input  E,
  input  [31:0] I_D__bus,
  input  [31:0] D_D__bus,
  input  [31:0] I_A__bus,
  input  [31:0] D_A__bus,
  input  INT_nor,
  input  INT_nmk,
  input  run,
  input  I_valid,
  input  D_valid,
  output I_LD,
  output D_LD,
  output D_ST,
  output [1:0] MMU_sel,
  output MMU_str,
  output [2:0] DMA_sel,
  output DMA_str,
  output INT_str,
  output CLK_str,
  output [1:0] CSH_mode,
  output CSH_run,
  output INT_out,
  output [1:0] D_MD
);

  wire add_4c32_1_c, alu_32_1_p6, alu_32_1_p9, ALU_A_CLR, ALU_A_CMP, ALU_A_DRD, ALU_A_FRD, ALU_A_LD,
       ALU_A_LRD, ALU_A_RE, ALU_A_STD, ALU_A_STF, ALU_B_CLR, ALU_B_CMP, ALU_B_DRD, ALU_B_FRD, ALU_B_LD,
       ALU_B_LRD, ALU_B_RE, ALU_B_STD, ALU_B_STF, ALU_busy, ALU_free, and_1_out, and_2_out, and_3_out,
       and_6_out, and_7_out, and_8_out, and_9_out, and_10_out, and_11_out, and_13_out, and_14_out,
       and_15_out, and_16_out, and_17_out, and_18_out, and_19_out, and_20_out, and_21_out, and_22_out,
       and_23_out, and_24_out, and_25_out, and_26_out, and_28_out, and_29_out, and_30_out, and_31_out,
       and_32_out, and_33_out, and_34_out, and_36_out, and_37_out, and_39_out, and_44_out, and_45_out,
       and_46_out, and_50_out, and_51_out, and_55_out, and_56_out, and_57_out, and_59_out, and_60_out,
       and_61_out, and_64_out, and_65_out, and_70_out, and_71_out, and_72_out, and_73_out, and_74_out,
       and_75_out, and_79_out, and_80_out, and_81_out, and_82_out, and_83_out, and_84_out, and_85_out,
       and_86_out, and_87_out, and_88_out, and_90_out, and_91_out, and_100_out, and_101_out, and_102_out,
       and_103_out, and_104_out, and_105_out, and_106_out, and_107_out, and_108_out, and_109_out,
       and_110_out, and_111_out, and_112_out, and_113_out, and_114_out, and_115_out, and_116_out,
       and_117_out, and_118_out, and_119_out, and_120_out, C_ct, C_dt, clr, clr_ep, cm_e, cm_e__bf, com1,
       com1_M, com2, comparator_1_gt, comparator_2_gt, comparator_2_lt, comparator_3_eq, comparator_4_eq,
       CT_ALU__LD, CT_ALU__M, CT_ALU__M2, CT_ALU__WD, CT_ALU__WF, CT_BUS__DAG, CT_BUS__DAM, CT_BUS__DAR,
       CT_BUS__DDG, CT_BUS__DDM, CT_BUS__DDR, CT_BUS__IAG, CT_BUS__IAR, CT_BUS__IDM, CT_BUS__IDR, CT_DEP__EA,
       CT_DEP__EB, CT_DIR__LD, CT_DIR__M, CT_DIR__MS, CT_DISP, CT_FL__W1, CT_FL__W2, CT_FU__EPOCH, CT_haz,
       CT_ISS__OFL, CT_ISS__OLDB, CT_ISS__ORC, CT_ISS__OSC, CT_ISS__OSTB, CT_ISS__UFL, CT_ISS__URA,
       CT_ISS__URB, CT_ISS__USC, CT_LDB__LD, CT_MB__LD, CT_MB__ST, CT_MVR, CT_RF__DM, CT_RF__E, CT_RF__FLS,
       CT_RF__PCAE, CT_RF__PCH, CT_RF__PCJ, CT_RF__PCR, CT_RF__PCSE, CT_RF__SCAE, CT_RF__SCAS, CT_RF__SCD,
       CT_RF__SCSE, CT_RF__W1, CT_RF__W2, CT_ROB__EX__E, CT_ROB__FL__STA, CT_ROB__FL__STB, CT_ROB__GEN__STA,
       CT_ROB__GEN__STB, CT_ROB__ST__E, CT_rollback, CT_SC__D1, CT_SC__D2, CT_SC__W1, CT_SC__W2, CT_STB__LD,
       DC_B_q, dc_e, DC_q, dipswitch_1_out, dipswitch_2_out, dipswitch_3_out, dipswitch_4_out,
       dipswitch_5_out, DIR_busy, DIR_CLR, DIR_free, DIR_LD, DIR_RD, DIR_ST, dp_e, ecm_e__bf, epoch_DP,
       epoch_IS, ex_e, ex_e__bf, ex_nop, ft_e, FT_q, halt_FT_DC_ISS, hlt, id_full, id_manager_1_p9,
       inst_comp_1_a_old, inst_comp_2_a_old, inst_comp_3_a_old, inst_comp_4_a_old, inst_comp_5_a_old,
       inst_comp_6_a_old, inst_comp_8_a_old, inst_comp_9_a_old, int_run, ISS_B_q, issue, kernel_inst,
       LDB_busy, LDB_LD, LDB_ldV, LDB_M__EP, LDB_M__V, load_buffer_1_fl, load_buffer_1_fl_ep,
       load_buffer_1_v, MB_busy, MB_ep, MB_free, MB_LD, MB_ld__e, MB_st__e, MB_type__st, MEM_LD, MEM_LD__RD,
       MEM_RD, mode, multiplexer_5_out, multiplexer_6_out, multiplexer_10_out, multiplexer_11_out,
       multiplexer_14_out, multiplexer_15_out, multiplexer_16_out, multiplexer_18_out, multiplexer_19_out,
       multiplexer_20_out, multiplexer_26_out, multiplexer_28_out, multiplexer_31_out, multiplexer_32_out,
       multiplexer_33_out, multiplexer_41_out, multiplexer_46_out, multiplexer_47_out, multiplexer_51_out,
       multiplexer_54_out, multiplexer_55_out, multiplexer_56_out, multiplexer_57_out, multiplexer_58_out,
       multiplexer_59_out, multiplexer_60_out, multiplexer_61_out, multiplexer_63_out, multiplexer_67_out,
       multiplexer_68_out, multiplexer_72_out, multiplexer_75_out, multiplexer_76_out, multiplexer_77_out,
       multiplexer_78_out, multiplexer_82_out, multiplexer_83_out, nand_16_out, nor_1_out, nor_2_out,
       nor_5_out, not_1_out, not_3_out, not_7_out, not_8_out, not_9_out, not_11_out, not_12_out, not_13_out,
       not_14_out, not_16_out, not_18_out, not_19_out, not_20_out, not_21_out, not_22_out, not_23_out,
       not_29_out, not_30_out, not_31_out, not_32_out, not_33_out, or_3_out, or_4_out, or_13_out, or_15_out,
       or_16_out, or_17_out, or_18_out, or_21_out, or_22_out, or_23_out, or_25_out, or_27_out, or_28_out,
       or_29_out, or_30_out, or_32_out, or_36_out, or_37_out, or_40_out, or_41_out, or_42_out, or_43_out,
       or_44_out, or_45_out, or_46_out, or_47_out, or_49_out, or_50_out, or_51_out, or_52_out, or_53_out,
       pc_ov, register_9_q, register_18_q, register_21_q, register_22_q, register_23_q, register_30_q,
       register_31_q, register_32_q, register_39_q, register_43_q, register_44_q, register_48_q,
       register_53_q, register_54_q, register_55_q, register_60_q, register_67_q, register_71_q,
       register_72_q, register_76_q, register_82_q, register_95_q, register_101_q, register_102_q,
       register_103_q, register_104_q, register_105_q, register_106_q, register_107_q, register_108_q,
       res_station_1_p2, rf_e, rs_ff_1_nq, rs_ff_3_nq, rs_ff_4_nq, rs_ff_5_nq, rs_ff_6_nq, rs_ff_7_nq,
       rs_ff_13_q, rs_ff_14_q, rs_ff_15_q, rs_ff_16_q, RS_full, sc_ov, st, st_e__bf, STB_busy, STB_M__EP,
       STB_M__V, xor_1_out, xor_9_out;
  wire [0:0] and_49_out, and_52_out;
  wire [1:0] and_66_out, and_68_out, CT_ALU__M_old, d_ff_1_q, d_ff_2_q, LDB_M__MD, MB_MD, multiplexer_8_out,
       multiplexer_53_out, multiplexer_74_out, or_14_out, register_12_q, register_50_q, register_78_q,
       STB_M__MD;
  wire [1:1] d_ff_3_q, d_ff_4_q, register_56_q, register_79_q, register_80_q;
  wire [2:0] ALU_A_RM, ALU_B_RM, and_43_out, and_48_out, and_58_out, and_62_out, and_63_out, CT_BUS__DASDN,
       CT_DEP__UMA, CT_DEP__UMB, CT_ISS__UFU, CT_RF__MA, CT_RF__MB, CT_RF__SCN, CT_RF__WM, CT_SC__O1,
       CT_SC__O2, multiplexer_13_out, multiplexer_29_out, multiplexer_39_out, multiplexer_44_out, nand_1_out,
       nand_2_out, nand_4_out, nand_5_out, nand_10_out, nand_11_out, not_10_out, not_15_out, not_17_out,
       register_16_q, register_17_q, register_19_q, register_51_q, register_52_q, register_57_q,
       register_58_q, store_controller_1_d1_sel, store_controller_1_d2_sel, store_controller_2_d1_sel,
       store_controller_2_d2_sel;
  wire [2:1] and_47_out;
  wire [3:0] ALU_A_INST, ALU_B_INST, clr_id, com1_inst, com2_inst, CT_FU__INST, DIR_INST, inst_DP, inst_EX,
       inst_EXT, inst_IS, inst_ST, LD_id, LDB_M__ID, load_buffer_1_fl_id, load_buffer_1_id_o, MB_INST,
       MB_INSt_t, MEM_INST, MEM_LD__INST, multiplexer_3_out, multiplexer_17_out, multiplexer_30_out,
       multiplexer_40_out, multiplexer_45_out, multiplexer_52_out, multiplexer_62_out, multiplexer_66_out,
       multiplexer_73_out, multiplexer_81_out, register_20_q, register_29_q, register_38_q, register_42_q,
       register_49_q, register_66_q, register_70_q, register_77_q, ROB_FL_INSTA, ROB_FL_INSTB, ROB_GEN_INSTA,
       ROB_GEN_INSTB, STB_M__ID;
  wire [3:3] register_17_q_2;
  wire [4:0] CT_DEP__URA, CT_DEP__URB, CT_ISS__RA, CT_ISS__RB, CT_ISS__RC, CT_RF__RA, CT_RF__RB, CT_RF__WS;
  wire [7:0] ALU_A_F, ALU_A_FI, ALU_A_T__F, ALU_B_F, ALU_B_FI, ALU_B_T__F, bitextender_2_out, byte_D0,
       byte_D0_iv, byte_D1, byte_D1_ex, byte_D1_st, byte_D2, byte_D2_ex, byte_D3, byte_D3_ex, byte_I0,
       byte_I0_iv, byte_I1, byte_I2, byte_I3, CT_FL__D1, CT_FL__D2, CT_FU__WR, CT_RF__R1, CT_RF__R2, DIR_WR,
       fl_i, FU_free, multiplexer_4_out, multiplexer_23_out, multiplexer_25_out, multiplexer_36_out,
       multiplexer_38_out, multiplexer_43_out, multiplexer_65_out, register_26_q, register_28_q,
       register_35_q, register_37_q, register_41_q, register_69_q, ROB_FL_A, ROB_FL_B, ROB_GEN_WA,
       ROB_GEN_WB, xor_2_out;
  wire [7:3] ALU_A_WR, ALU_B_WR;
  wire [8:0] ALU_A_CT, ALU_B_CT, CT_ALU__CT, multiplexer_24_out, multiplexer_37_out, register_27_q,
       register_36_q;
  wire [9:0] and_12_out;
  wire [15:0] bitextender_3_out, IV_inst, multiplexer_50_out, multiplexer_71_out, register_47_q,
       register_75_q, register_90_q, V_inst;
  wire [31:0] add_1_s, add_4c32_1_s, alu_32_1_p8, alu_32_1_p11, alu_32_1_p12, alu_32_1_p14, ALU_A_A, ALU_A_B,
       ALU_A_R, ALU_A_T__R, ALU_B_A, ALU_B_B, ALU_B_R, ALU_B_T__R, bitextender_1_out, CT_RF__D1, CT_RF__D2,
       DIR, FL, I_A__R_q, I_D__R_q, LD_addr, LDB_ldD, LDB_M__A, load_buffer_1_d_o, MB_addr, MB_data,
       MEM_LD__D, multiplexer_2_out, multiplexer_7_out, multiplexer_12_out, multiplexer_21_out,
       multiplexer_22_out, multiplexer_27_out, multiplexer_34_out, multiplexer_35_out, multiplexer_42_out,
       multiplexer_48_out, multiplexer_49_out, multiplexer_64_out, multiplexer_69_out, multiplexer_70_out,
       multiplexer_80_out, mVec, pc_read, PCA, pca_i, PCS, PCS_DC, PCS_FT, pcs_i, PCS_IS, R_A, R_B,
       ramdualaccess_1_d1, ramdualaccess_1_d2, register_4_q, register_11_q, register_13_q, register_24_q,
       register_25_q, register_33_q, register_34_q, register_40_q, register_45_q, register_46_q,
       register_68_q, register_73_q, register_74_q, register_89_q, ROB_GEN_DA, ROB_GEN_DB, SCA, sca_i, SCS,
       scs_i, STB_M__A, STB_M__D;
  wire [31:24] res_station_1_p32;

  Comparator #(.Bits(32)) comparator_1 (.a(PCS), .b(mVec), .gt(comparator_1_gt));  // open: eq, lt
  BitExtender #(.inputBits(16), .outputBits(32)) bitextender_1 (.in({byte_D2_ex, byte_D3_ex}), .out(bitextender_1_out));
  and and_1 (and_1_out, FL[14], INT_nor);
  and and_2 (and_2_out, 1'b0, ~comparator_1_gt);  // And
  Add #(.Bits(32)) add_1 (.a(R_A), .b(bitextender_1_out), .c_i(1'b0), .s(add_1_s));  // open: c_o
  or or_1 (int_run, and_1_out, INT_nmk);
  RS_FF u_mode (.S(and_2_out), .C(C_dt), .R(comparator_1_gt), .Q(mode));  // open: nQ
  Register #(.Bits(32)) MVR (.D(add_1_s), .C(C_dt), .en(CT_MVR), .Q(mVec));
  PullDown pulldown_1 (.out(CT_haz));
  // id_manager id_manager_1: pin names not known; wires that end beside it: C_ct, issue, V_inst, clr, clr_ep, clr_id, epoch_IS, inst_IS, id_manager_1_p9, com1, com1_inst, com2, com2_inst
  and and_3 (and_3_out, CT_haz, dp_e);
  assign CT_RF__PCSE = ft_e ? 1'b1 : 1'bz;  // Driver driver_1
  assign CT_BUS__IAR = ft_e ? 1'b1 : 1'bz;  // Driver driver_2
  assign CT_BUS__IAG = ft_e ? 1'b1 : 1'bz;  // Driver driver_3
  assign I_LD = ft_e ? 1'b1 : 1'bz;  // Driver driver_4
  RS_FF FT (.S(run), .C(C_ct), .R(hlt), .Q(FT_q));  // open: nQ
  not not_1 (not_1_out, and_3_out);
  assign ex_nop = and_3_out ? 1'b1 : 1'bz;  // Driver driver_5
  not not_2 (id_full, id_manager_1_p9);
  and and_4 (ft_e, FT_q, not_1_out);
  Register DC_B (.D(FT_q), .C(C_dt), .en(1'b1), .Q(DC_B_q));
  Register #(.Bits(32)) register_1 (.D(PCS), .C(C_dt), .en(CT_RF__PCSE), .Q(PCS_FT));
  Register DC (.D(FT_q), .C(C_ct), .en(1'b1), .Q(DC_q));
  not not_3 (not_3_out, I_valid);
  assign CT_BUS__IDM = not_3_out ? 1'b1 : 1'bz;  // Driver driver_6
  DipSwitch dipswitch_1 (.out(dipswitch_1_out));
  Multiplexer multiplexer_1 (.sel(dipswitch_2_out), .in_0(dipswitch_1_out), .in_1(C), .out(C_dt));
  DipSwitch dipswitch_2 (.out(dipswitch_2_out));
  not not_4 (C_ct, C_dt);
  and and_5 (dc_e, DC_q, not_1_out);
  Register ISS_B (.D(DC_B_q), .C(C_dt), .en(1'b1), .Q(ISS_B_q));
  Register #(.Bits(32)) register_2 (.D(PCS_FT), .C(C_dt), .en(CT_RF__PCSE), .Q(PCS_DC));
  Multiplexer #(.Bits(32)) multiplexer_2 (.sel(CT_RF__DM), .in_0(ALU_A_T__R), .in_1(D_D__bus), .out(multiplexer_2_out));
  and and_6 (and_6_out, rf_e, CT_RF__E);
  Register ISS (.D(DC_q), .C(C_ct), .en(1'b1), .Q(dp_e));
  // Probe on multiplexer_2_out
  // Probe on CT_RF__WS
  // Probe on CT_RF__WM
  // Probe on CT_RF__RA
  // Probe on CT_RF__MA
  // Probe on CT_RF__RB
  // Probe on CT_RF__MB
  Register EX_B (.D(ISS_B_q), .C(C_dt), .en(1'b1), .Q(ex_e__bf));
  Register #(.Bits(32)) register_3 (.D(PCS_DC), .C(C_dt), .en(CT_RF__PCSE), .Q(PCS_IS));
  Register #(.Bits(4)) EX (.D(inst_DP), .C(C_dt), .en(dp_e), .Q(inst_EX));
  PullDown pulldown_2 (.out(CT_DISP));
  PullDown pulldown_3 (.out(CT_rollback));
  PullDown pulldown_4 (.out(com2));
  PullDown #(.Bits(4)) pulldown_5 (.out(com2_inst));
  PullDown pulldown_6 (.out(com1_M));
  PullDown pulldown_7 (.out(com1));
  PullDown #(.Bits(4)) pulldown_8 (.out(com1_inst));
  Register #(.Bits(32)) register_4 (.D(multiplexer_2_out), .C(C_dt), .en(and_6_out), .Q(register_4_q));
  // Probe on and_6_out
  // Probe INST on {byte_I0, byte_I1, byte_I2, byte_I3}
  Register EX_2 (.D(dp_e), .C(C_ct), .en(1'b1), .Q(ex_e));
  // Probe on register_4_q
  assign byte_I0_iv = ~byte_I0;  // Not not_5, 8 bits wide
  assign byte_D0_iv = ~byte_D0;  // Not not_6, 8 bits wide
  Register ST_B (.D(ex_e__bf), .C(C_dt), .en(1'b1), .Q(st_e__bf));
  Register #(.Bits(4)) u_ST (.D(inst_EX), .C(C_dt), .en(ex_e), .Q(inst_ST));
  // Probe inst on {byte_I0, byte_I1, byte_I2, byte_I3}
  // Probe R_A on R_A
  // Probe R_B on R_B
  // Probe PC on PCS
  // Probe SC on SCS
  // Probe FL on FL
  // Probe CT_BUS-_IDM on CT_BUS__IDM
  // Probe C_i on C_dt
  Register ST_2 (.D(ex_e), .C(C_ct), .en(1'b1), .Q(rf_e));
  Register #(.Bits(4)) EXT (.D(inst_ST), .C(C_dt), .en(rf_e), .Q(inst_EXT));
  Register CM_B___EXT_B (.D(st_e__bf), .C(C_dt), .en(1'b1), .Q(cm_e__bf));
  Register CM___EXT (.D(rf_e), .C(C_ct), .en(1'b1), .Q(cm_e));
  // Probe com1_inst on com1_inst
  // Probe com2_inst on com2_inst
  // Probe inst_ST on inst_ST
  // Probe PC_inst on inst_IS
  // Probe inst_EX on inst_EX
  Register #(.Bits(8)) register_5 (.D(byte_D1), .C(C_ct), .en(ex_e__bf), .Q(byte_D1_ex));
  Register #(.Bits(8)) register_6 (.D(byte_D2), .C(C_ct), .en(ex_e__bf), .Q(byte_D2_ex));
  Register #(.Bits(8)) register_7 (.D(byte_D3), .C(C_ct), .en(ex_e__bf), .Q(byte_D3_ex));
  Register EXT_CM_B (.D(cm_e__bf), .C(C_dt), .en(1'b1), .Q(ecm_e__bf));
  or or_2 (halt_FT_DC_ISS, RS_full, id_full);
  RAMDualAccess #(.AddrBits(24), .isProgramMemory("true"), .Bits(32)) ramdualaccess_1 (
    .str(D_ST), .C(C_dt), .ld(1'b1), .A1(D_A__bus[25:2]), .Din1(D_D__bus), .A2(I_A__bus[25:2]),
    .D1(ramdualaccess_1_d1), .D2(ramdualaccess_1_d2));
  assign D_D__bus = D_LD ? ramdualaccess_1_d1 : 32'bz;  // Driver driver_7
  assign I_D__bus = I_LD ? ramdualaccess_1_d2 : 32'bz;  // Driver driver_8
  Register #(.Bits(8)) register_8 (.D(byte_D1_ex), .C(C_ct), .en(st_e__bf), .Q(byte_D1_st));
  Multiplexer #(.Bits(4)) multiplexer_3 (.sel(com2), .in_0(com1_inst), .in_1(com2_inst), .out(multiplexer_3_out));
  ROB_gen rob_gen_1 (
    .D1_O(CT_RF__D1), .R1_O(CT_RF__R1), .W1_O(CT_RF__W1), .D2_O(CT_RF__D2), .R2_O(CT_RF__R2),
    .W2_O(CT_RF__W2), .C(C_dt), .E1(CT_ROB__GEN__STA), .E2(CT_ROB__GEN__STB), .D1(ROB_GEN_DA),
    .D2(ROB_GEN_DB), .R1(ROB_GEN_WA), .R2(ROB_GEN_WB), .inst1(ROB_GEN_INSTA), .inst2(ROB_GEN_INSTB),
    .com1(com1), .com2(com2), .com1_id(com1_inst), .com2_id(com2_inst));
  ROB_PC rob_pc_1 (
    .C(C_dt), .E(issue), .D(PCS_DC), .inst(inst_IS), .com_id(multiplexer_3_out), .read_id(inst_DP),
    .D1(pca_i), .D2(pc_read));
  ROB_SC rob_sc_1 (
    .C(C_dt), .E(CT_RF__SCSE), .dec(CT_RF__SCD), .off(CT_RF__SCN), .inst(inst_DP), .com1(com1), .com2(com2),
    .com1_id(com1_inst), .com2_id(com2_inst), .W1(CT_SC__W1), .dec1(CT_SC__D1), .off1(CT_SC__O1),
    .W2(CT_SC__W2), .dec2(CT_SC__D2), .off2(CT_SC__O2));
  ROB_FL rob_fl_1 (
    .C(C_dt), .E1(CT_ROB__FL__STA), .E2(CT_ROB__FL__STB), .D1(ALU_A_T__F), .D2(ALU_B_T__F),
    .inst1(ROB_FL_INSTA), .inst2(ROB_FL_INSTB), .com1(com1), .com2(com2), .com1_id(com1_inst),
    .com2_id(com2_inst), .W1_O(CT_FL__W1), .D1_O(CT_FL__D1), .W2_O(CT_FL__W2), .D2_O(CT_FL__D2));
  PullDown pulldown_9 (.out(D_valid));
  or or_3 (or_3_out, STB_M__V, LDB_M__V);
  RS_FF rs_ff_1 (.S(MEM_LD), .C(C_ct), .R(D_valid), .Q(MEM_RD), .nQ(rs_ff_1_nq));
  and and_7 (and_7_out, byte_D0[3], byte_D0[0]);
  and and_8 (and_8_out, byte_D0[2], byte_D0[0]);
  and and_9 (and_9_out, byte_D0_iv[3], byte_D0_iv[2], byte_D0[1], byte_D0_iv[0]);
  and and_10 (and_10_out, byte_D0_iv[4], byte_D0[3], byte_D0[2], byte_D0[1]);
  and and_11 (and_11_out, byte_D0[4], byte_D0_iv[3], byte_D0_iv[2], byte_D0[1], byte_D0[0]);
  and and_12 (and_12_out[7], byte_D0_iv[4], byte_D0[3], byte_D0[2]);
  and and_13 (and_13_out, byte_D0[4], byte_D0[2], byte_D0_iv[1]);
  and and_14 (and_14_out, byte_D0[4], byte_D0_iv[3], byte_D0_iv[2]);
  and and_15 (and_15_out, byte_D0_iv[4], byte_D0_iv[3], byte_D0_iv[2]);
  and and_16 (and_16_out, byte_D0_iv[4], byte_D0_iv[3]);
  and and_17 (and_17_out, byte_D0_iv[4], byte_D0[3], byte_D0_iv[2], byte_D0_iv[1]);
  and and_18 (and_18_out, byte_D0_iv[4], byte_D0[3], byte_D0_iv[2]);
  and and_19 (and_19_out, byte_D0[4], byte_D0[3]);
  and and_20 (and_20_out, byte_D0_iv[4], byte_D0_iv[3], byte_D0[2], byte_D0_iv[1]);
  and and_21 (and_21_out, byte_D0[4], byte_D0[2], byte_D0[1]);
  and and_22 (and_22_out, byte_D0_iv[4], byte_D0_iv[3], byte_D0_iv[2], byte_D0[1], byte_D0[0]);
  and and_23 (and_23_out, byte_D0_iv[2], byte_D0_iv[0]);
  and and_24 (and_24_out, byte_D0[2], byte_D0[0]);
  and and_25 (and_25_out, byte_D0[1], byte_D0[2], byte_D0[4]);
  and and_26 (and_26_out, byte_D0[3], byte_D0[4]);
  or or_4 (or_4_out, rs_ff_1_nq, D_valid);
  or or_5 (and_12_out[9], and_7_out, and_8_out, and_9_out);
  or or_6 (and_12_out[6], and_13_out, and_10_out, and_11_out);
  or or_7 (and_12_out[5], and_12_out[7], and_13_out, and_14_out);
  or or_8 (and_12_out[4], and_20_out, and_21_out, and_15_out);
  or or_9 (and_12_out[3], and_16_out, and_21_out, and_17_out);
  or or_10 (and_12_out[2], and_18_out, and_19_out);
  or or_11 (and_12_out[1], and_20_out, and_21_out, and_22_out);
  or or_12 (and_12_out[0], byte_D0[3], byte_D0[1], and_23_out, and_24_out);
  nor nor_1 (nor_1_out, and_25_out, and_26_out);
  xor xor_1 (xor_1_out, STB_M__EP, LDB_M__EP);
  Comparator #(.Bits(4)) comparator_2 (
    .a(STB_M__ID), .b(LDB_M__ID), .gt(comparator_2_gt), .lt(comparator_2_lt));  // open: eq
  and and_27 (MEM_LD, or_3_out, or_4_out);
  and and_28 (and_28_out, ft_e, CT_BUS__IAR);
  Multiplexer #(.Bits(8)) multiplexer_4 (
    .sel(CT_BUS__IDM), .in_0(I_D__bus[31:24]), .in_1(8'h72), .out(multiplexer_4_out));
  and and_29 (and_29_out, STB_M__V, LDB_M__V);
  Multiplexer multiplexer_5 (.sel(xor_1_out), .in_0(comparator_2_gt), .in_1(comparator_2_lt), .out(multiplexer_5_out));
  and and_30 (and_30_out, byte_D0_iv[0], byte_D0_iv[1], byte_D0[2], byte_D0[3], byte_D0[4], byte_D0_iv[5], byte_D0_iv[6], byte_D0_iv[7]);
  and and_31 (and_31_out, byte_D0[1], byte_D0_iv[2], byte_D0[3], byte_D0[4], byte_D0_iv[5], byte_D0_iv[6], byte_D0_iv[7]);
  and and_32 (and_32_out, com1, CT_RF__W1);
  and and_33 (and_33_out, com2, CT_RF__W2);
  Multiplexer multiplexer_6 (.sel(and_29_out), .in_0(STB_M__V), .in_1(multiplexer_5_out), .out(multiplexer_6_out));
  and and_34 (and_34_out, byte_D0[4], byte_D0[3], byte_D0_iv[1], byte_D0_iv[2], byte_D0_iv[5], byte_D0_iv[6], byte_D0_iv[7]);
  or or_13 (or_13_out, and_30_out, and_31_out);
  PullDown #(.Bits(16)) pulldown_10 (.out(V_inst));
  PullDown #(.Bits(16)) pulldown_11 (.out(IV_inst));
  or or_14 (or_14_out[1], CT_RF__PCH, CT_RF__PCR);
  and and_35 (or_14_out[0], ~CT_RF__PCH, CT_RF__PCJ);  // And
  nor nor_2 (nor_2_out, CT_RF__PCR, CT_RF__PCJ);
  Register #(.Bits(32)) I_A__R (.D(PCS), .C(C_dt), .en(and_28_out), .Q(I_A__R_q));
  Register #(.Bits(32)) I_D__R (.D({multiplexer_4_out, I_D__bus[23:0]}), .C(C_dt), .en(dc_e), .Q(I_D__R_q));
  Multiplexer #(.Bits(32)) multiplexer_7 (
    .sel(multiplexer_6_out), .in_0(LDB_M__A), .in_1(STB_M__A), .out(multiplexer_7_out));
  Multiplexer #(.Bits(2)) multiplexer_8 (
    .sel(multiplexer_6_out), .in_0(LDB_M__MD), .in_1(STB_M__MD), .out(multiplexer_8_out));
  regFile4 regfile4_1 (
    .C(C_dt), .E1(and_32_out), .E2(and_33_out), .D1(CT_RF__D1), .D2(CT_RF__D2), .RW1(CT_RF__R1[7:3]),
    .MW1(CT_RF__R1[2:0]), .RW2(CT_RF__R2[7:3]), .MW2(CT_RF__R2[2:0]), .RA(CT_RF__RA), .MA(CT_RF__MA),
    .RB(CT_RF__RB), .MB(CT_RF__MB), .PCS_i(pcs_i), .PCS_e(CT_RF__PCSE), .PCA_i(pca_i), .PCA_e(CT_RF__PCAE),
    .SCS_i(scs_i), .SCS_e(CT_RF__SCSE), .SCA_i(sca_i), .SCA_sel(CT_RF__SCAS), .SCA_e(CT_RF__SCAE),
    .FL_i({{24{1'b0}}, fl_i}), .FL_sel(CT_RF__FLS), .FL_e(4'b0001), .PC_read(pc_read), .R_A(R_A), .R_B(R_B),
    .PCS_O(PCS), .PCA_O(PCA), .SCS_O(SCS), .SCA_O(SCA), .FL_O(FL));
  add_4c32 add_4c32_1 (.a(PCS), .b(4'b0100), .s(add_4c32_1_s), .c(add_4c32_1_c));
  assign I_A__bus = and_39_out ? I_A__R_q : 32'bz;  // Driver driver_9
  Register register_9 (.D(multiplexer_6_out), .C(C_dt), .en(MEM_LD), .Q(register_9_q));
  Register #(.Bits(4)) register_10 (.D(LDB_M__ID), .C(C_dt), .en(MEM_LD), .Q(MEM_INST));
  Register #(.Bits(32)) register_11 (.D(multiplexer_7_out), .C(C_dt), .en(MEM_LD), .Q(register_11_q));
  Register #(.Bits(2)) register_12 (.D(multiplexer_8_out), .C(C_dt), .en(MEM_LD), .Q(register_12_q));
  Register #(.Bits(32)) register_13 (.D(STB_M__D), .C(C_dt), .en(MEM_LD), .Q(register_13_q));
  RS_FF rs_ff_2 (.S(1'b0), .C(C_ct), .R(D_valid), .nQ(MEM_LD__RD));  // open: Q
  Register #(.Bits(32)) register_14 (.D(D_D__bus), .C(C_dt), .en(D_valid), .Q(MEM_LD__D));
  Register #(.Bits(4)) register_15 (.D(MEM_INST), .C(C_dt), .en(D_valid), .Q(MEM_LD__INST));
  and and_36 (and_36_out, byte_D0_iv[7], byte_D0_iv[6], byte_D0_iv[5], byte_D0_iv[4]);
  and and_37 (and_37_out, byte_D0_iv[7], byte_D0_iv[6], byte_D0_iv[5], byte_D0[4], byte_D0_iv[3]);
  assign {CT_RF__RA, CT_RF__MA} = or_15_out ? byte_D1 : 8'bz;  // Driver driver_10
  assign {CT_RF__RB, CT_RF__MB} = or_15_out ? byte_D2 : 8'bz;  // Driver driver_11
  assign CT_ALU__LD = or_15_out ? 1'b1 : 1'bz;  // Driver driver_12
  assign CT_ALU__CT = or_15_out ? {1'b0, and_12_out[7:0]} : 9'bz;  // Driver driver_13
  assign CT_ALU__M = or_15_out ? and_12_out[9] : 1'bz;  // Driver driver_14
  assign CT_FU__INST = or_15_out ? inst_DP : 4'bz;  // Driver driver_15
  assign CT_FU__WR = or_15_out ? byte_D1 : 8'bz;  // Driver driver_16
  assign CT_ALU__WD = or_15_out ? nor_1_out : 1'bz;  // Driver driver_17
  assign CT_ALU__WF = or_15_out ? 1'b1 : 1'bz;  // Driver driver_18
  assign {CT_RF__RB, CT_RF__MB} = or_13_out ? byte_D2 : 8'bz;  // Driver driver_19
  assign CT_DIR__LD = or_13_out ? 1'b1 : 1'bz;  // Driver driver_20
  assign CT_DIR__M = or_13_out ? and_31_out : 1'bz;  // Driver driver_21
  assign CT_DIR__MS = or_13_out ? byte_D0[0] : 1'bz;  // Driver driver_22
  assign CT_FU__INST = or_13_out ? inst_DP : 4'bz;  // Driver driver_23
  assign CT_FU__WR = or_13_out ? byte_D1 : 8'bz;  // Driver driver_24
  PullDown pulldown_12 (.out(CT_RF__PCAE));
  PullDown pulldown_13 (.out(CT_RF__SCAE));
  Multiplexer #(.Selector_Bits(2), .Bits(32)) multiplexer_9 (
    .sel(or_14_out), .in_0(add_4c32_1_s), .in_1(ALU_A_T__R), .in_2(PCA), .in_3(D_D__bus), .out(pcs_i));
  and and_38 (pc_ov, add_4c32_1_c, nor_2_out);
  and and_39 (and_39_out, CT_BUS__IAG, bus_e);
  D_FF #(.Bits(32)) INST_3 (.D(I_D__R_q), .C(C_ct), .Q({byte_I0, byte_I1, byte_I2, byte_I3}));  // open: nQ
  assign D_A__bus = MEM_RD ? register_11_q : 32'bz;  // Driver driver_25
  assign D_MD = MEM_RD ? register_12_q : 2'bz;  // Driver driver_26
  assign D_D__bus = MEM_RD ? register_13_q : 32'bz;  // Driver driver_27
  and and_40 (D_LD, ~register_9_q, MEM_RD);  // And
  and and_41 (D_ST, MEM_RD, register_9_q);
  or or_15 (or_15_out, and_36_out, and_34_out, and_37_out);
  BitExtender #(.inputBits(1), .outputBits(8)) bitextender_2 (.in(register_17_q_2[3]), .out(bitextender_2_out));
  assign xor_2_out = FL[7:0] ^ bitextender_2_out;  // XOr xor_2, 8 bits wide
  not not_7 (not_7_out, byte_D1_ex[1]);
  or or_16 (or_16_out, byte_D1_ex[2], byte_D1_ex[0]);
  and and_42 (and_43_out[2], byte_D0_iv[7], byte_D0_iv[6], byte_D0[5]);
  and and_43 (and_43_out[1], byte_D0_iv[7], byte_D0[6], byte_D0_iv[5]);
  or or_17 (or_17_out, byte_D1_ex[0], byte_D1_ex[2]);
  Multiplexer #(.Selector_Bits(3)) multiplexer_10 (
    .sel(register_17_q), .in_0(xor_2_out[0]), .in_1(xor_2_out[1]), .in_2(xor_2_out[2]), .in_3(xor_2_out[3]),
    .in_4(xor_2_out[4]), .in_5(xor_2_out[5]), .in_6(xor_2_out[6]), .in_7(xor_2_out[7]),
    .out(multiplexer_10_out));
  and and_44 (and_44_out, com1, CT_SC__W1);
  and and_45 (and_45_out, com2, CT_SC__W2);
  not not_8 (not_8_out, clr);
  and and_46 (and_46_out, byte_D2_ex[7], CT_DIR__MS);
  and and_47 (and_47_out[1], not_7_out, or_16_out);
  nor nor_3 (and_47_out[2], byte_D1_ex[2], byte_D1_ex[1], byte_D1_ex[0]);
  not not_9 (not_9_out, byte_D1_ex[1]);
  Multiplexer multiplexer_11 (.sel(and_58_out[2]), .in_0(nand_1_out[2]), .in_1(not_8_out), .out(multiplexer_11_out));
  not not_10 (not_10_out[0], register_19_q[0]);
  xor xor_3 (not_10_out[1], register_19_q[0], register_19_q[1]);
  xor xor_4 (not_10_out[2], register_19_q[1], register_19_q[2]);
  Multiplexer #(.Bits(32)) multiplexer_12 (
    .sel(CT_ALU__M), .in_0(R_B), .in_1({{16{1'b0}}, byte_D2_ex, byte_D3_ex}), .out(multiplexer_12_out));
  BitExtender #(.inputBits(1)) bitextender_3 (.in(and_46_out), .out(bitextender_3_out));
  or or_18 (or_18_out, CT_FU__WR[0], CT_FU__WR[2]);
  not not_11 (not_11_out, CT_FU__WR[1]);
  not not_12 (not_12_out, byte_D0[0]);
  and and_48 (and_48_out[0], byte_D0[1], byte_D0[2], byte_D0[3], byte_D0[4], byte_D0_iv[5], byte_D0_iv[6], byte_D0_iv[7]);
  Register #(.Bits(3)) register_16 (.D({and_47_out, byte_D1_ex[1]}), .C(C_ct), .en(st_e__bf), .Q(register_16_q));
  or or_19 (and_43_out[0], and_43_out[2], and_43_out[1]);
  and and_49 (and_49_out[0], or_17_out, not_9_out);
  and and_50 (and_50_out, byte_D0_iv[4], byte_D0[5], byte_D0[6], byte_D0_iv[7]);
  Comparator #(.Bits(3)) comparator_3 (.a(byte_D0[2:0]), .b(3'b110), .eq(comparator_3_eq));  // open: gt, lt
  Register #(.Bits(4)) register_17 (.D(byte_D0[3:0]), .C(C_ct), .en(ex_e__bf), .Q({register_17_q_2[3], register_17_q}));
  Register register_18 (.D(xor_9_out), .C(C_ct), .en(st_e__bf), .Q(register_18_q));
  or or_20 (CT_RF__SCAE, and_44_out, and_45_out);
  and and_51 (and_51_out, multiplexer_11_out, CT_ALU__LD);
  Register register_19 (.D(and_51_out), .C(C_ct), .en(or_21_out), .Q(register_19_q[2]));
  not not_13 (not_13_out, multiplexer_11_out);
  or or_21 (or_21_out, not_13_out, multiplexer_13_out[2]);
  Multiplexer #(.Bits(3)) multiplexer_13 (
    .sel(or_22_out), .in_0(not_10_out), .in_1(and_58_out), .out(multiplexer_13_out));
  or or_22 (or_22_out, and_58_out[0], and_58_out[1], and_58_out[2]);
  Register #(.Bits(4)) register_20 (.D(CT_FU__INST), .C(C_ct), .en(multiplexer_13_out[2]), .Q(register_20_q));
  Register register_21 (.D(CT_FU__EPOCH), .C(C_ct), .en(multiplexer_13_out[2]), .Q(register_21_q));
  Register register_22 (.D(CT_ALU__WD), .C(C_ct), .en(multiplexer_13_out[2]), .Q(register_22_q));
  Register register_23 (.D(CT_ALU__WF), .C(C_ct), .en(multiplexer_13_out[2]), .Q(register_23_q));
  Register #(.Bits(32)) register_24 (.D(R_A), .C(C_dt), .en(multiplexer_13_out[2]), .Q(register_24_q));
  Register #(.Bits(32)) register_25 (.D(multiplexer_12_out), .C(C_dt), .en(multiplexer_13_out[2]), .Q(register_25_q));
  Register #(.Bits(8)) register_26 (.D(FL[7:0]), .C(C_dt), .en(multiplexer_13_out[2]), .Q(register_26_q));
  Register #(.Bits(9)) register_27 (.D(CT_ALU__CT), .C(C_ct), .en(multiplexer_13_out[2]), .Q(register_27_q));
  Register #(.Bits(8)) register_28 (.D(CT_FU__WR), .C(C_ct), .en(multiplexer_13_out[2]), .Q(register_28_q));
  and and_52 (and_52_out[0], or_18_out, not_11_out);
  and and_53 (and_48_out[1], and_48_out[0], byte_D0[0]);
  and and_54 (and_48_out[2], not_12_out, and_48_out[0]);
  Multiplexer multiplexer_14 (.sel(ex_nop), .in_0(and_50_out), .in_1(1'b0), .out(multiplexer_14_out));
  assign st = register_18_q ? 1'b1 : 1'bz;  // Driver driver_28
  Multiplexer multiplexer_15 (
    .sel(and_58_out[1]), .in_0(nand_1_out[1]), .in_1(nand_1_out[2]), .out(multiplexer_15_out));
  Multiplexer multiplexer_16 (
    .sel(register_19_q[2]), .in_0(CT_ALU__LD), .in_1(register_19_q[2]), .out(multiplexer_16_out));
  Multiplexer #(.Bits(4)) multiplexer_17 (
    .sel(register_19_q[2]), .in_0(CT_FU__INST), .in_1(register_20_q), .out(multiplexer_17_out));
  inst_comp inst_comp_1 (
    .A_id(register_20_q), .A_ep(register_21_q), .B_id(clr_id), .B_ep(clr_ep), .A_old(inst_comp_1_a_old));
  Multiplexer multiplexer_18 (
    .sel(register_19_q[2]), .in_0(CT_FU__EPOCH), .in_1(register_21_q), .out(multiplexer_18_out));
  Multiplexer multiplexer_19 (
    .sel(register_19_q[2]), .in_0(CT_ALU__WD), .in_1(register_22_q), .out(multiplexer_19_out));
  Multiplexer multiplexer_20 (
    .sel(register_19_q[2]), .in_0(CT_ALU__WF), .in_1(register_23_q), .out(multiplexer_20_out));
  Multiplexer #(.Bits(32)) multiplexer_21 (
    .sel(register_19_q[2]), .in_0(R_A), .in_1(register_24_q), .out(multiplexer_21_out));
  Multiplexer #(.Bits(32)) multiplexer_22 (
    .sel(register_19_q[2]), .in_0(multiplexer_12_out), .in_1(register_25_q), .out(multiplexer_22_out));
  Multiplexer #(.Bits(8)) multiplexer_23 (
    .sel(register_19_q[2]), .in_0(FL[7:0]), .in_1(register_26_q), .out(multiplexer_23_out));
  Multiplexer #(.Bits(9)) multiplexer_24 (
    .sel(register_19_q[2]), .in_0(CT_ALU__CT), .in_1(register_27_q), .out(multiplexer_24_out));
  Multiplexer #(.Bits(8)) multiplexer_25 (
    .sel(register_19_q[2]), .in_0(CT_FU__WR), .in_1(register_28_q), .out(multiplexer_25_out));
  Multiplexer multiplexer_26 (.sel(and_62_out[2]), .in_0(nand_4_out[2]), .in_1(not_14_out), .out(multiplexer_26_out));
  not not_14 (not_14_out, clr);
  not not_15 (not_15_out[0], register_57_q[0]);
  xor xor_5 (not_15_out[1], register_57_q[0], DIR_LD);
  xor xor_6 (not_15_out[2], DIR_LD, register_57_q[2]);
  Multiplexer #(.Bits(32)) multiplexer_27 (
    .sel(CT_DIR__M), .in_0(R_A), .in_1({bitextender_3_out, byte_D2_ex, byte_D3_ex}), .out(multiplexer_27_out));
  Multiplexer multiplexer_28 (.sel(and_63_out[2]), .in_0(nand_5_out[2]), .in_1(not_16_out), .out(multiplexer_28_out));
  not not_16 (not_16_out, clr);
  not not_17 (not_17_out[0], register_58_q[0]);
  xor xor_7 (not_17_out[1], register_58_q[0], register_58_q[1]);
  xor xor_8 (not_17_out[2], register_58_q[1], register_58_q[2]);
  not not_18 (not_18_out, comparator_3_eq);
  xor xor_9 (xor_9_out, multiplexer_54_out, register_53_q);
  and and_55 (and_55_out, multiplexer_15_out, multiplexer_16_out);
  not not_19 (not_19_out, multiplexer_15_out);
  or or_23 (or_23_out, not_19_out, multiplexer_13_out[1]);
  or or_24 (register_19_q[1], register_56_q[1], register_19_q[2]);
  nand nand_1 (nand_1_out[2], inst_comp_1_a_old, clr);
  Register #(.Bits(4)) register_29 (.D(multiplexer_17_out), .C(C_ct), .en(multiplexer_13_out[1]), .Q(register_29_q));
  Register register_30 (.D(multiplexer_18_out), .C(C_ct), .en(multiplexer_13_out[1]), .Q(register_30_q));
  Register register_31 (.D(multiplexer_19_out), .C(C_ct), .en(multiplexer_13_out[1]), .Q(register_31_q));
  Register register_32 (.D(multiplexer_20_out), .C(C_ct), .en(multiplexer_13_out[1]), .Q(register_32_q));
  Register #(.Bits(32)) register_33 (.D(multiplexer_21_out), .C(C_dt), .en(multiplexer_13_out[1]), .Q(register_33_q));
  Register #(.Bits(32)) register_34 (.D(multiplexer_22_out), .C(C_dt), .en(multiplexer_13_out[1]), .Q(register_34_q));
  Register #(.Bits(8)) register_35 (.D(multiplexer_23_out), .C(C_dt), .en(multiplexer_13_out[1]), .Q(register_35_q));
  Register #(.Bits(9)) register_36 (.D(multiplexer_24_out), .C(C_ct), .en(multiplexer_13_out[1]), .Q(register_36_q));
  Register #(.Bits(8)) register_37 (.D(multiplexer_25_out), .C(C_ct), .en(multiplexer_13_out[1]), .Q(register_37_q));
  and and_56 (and_56_out, multiplexer_26_out, CT_DIR__LD);
  not not_20 (not_20_out, multiplexer_26_out);
  or or_25 (or_25_out, not_20_out, multiplexer_39_out[2]);
  Register #(.Bits(4)) register_38 (.D(CT_FU__INST), .C(C_ct), .en(multiplexer_39_out[2]), .Q(register_38_q));
  Register register_39 (.D(CT_FU__EPOCH), .C(C_ct), .en(multiplexer_39_out[2]), .Q(register_39_q));
  Register #(.Bits(32)) register_40 (.D(multiplexer_27_out), .C(C_dt), .en(multiplexer_39_out[2]), .Q(register_40_q));
  Register #(.Bits(8)) register_41 (.D(CT_FU__WR), .C(C_ct), .en(multiplexer_39_out[2]), .Q(register_41_q));
  and and_57 (and_57_out, multiplexer_28_out, CT_MB__LD);
  not not_21 (not_21_out, multiplexer_28_out);
  Register #(.Bits(4)) register_42 (.D(CT_FU__INST), .C(C_ct), .en(multiplexer_44_out[2]), .Q(register_42_q));
  Register register_43 (.D(CT_FU__EPOCH), .C(C_ct), .en(multiplexer_44_out[2]), .Q(register_43_q));
  Register register_44 (.D(CT_MB__ST), .C(C_ct), .en(multiplexer_44_out[2]), .Q(register_44_q));
  Register #(.Bits(32)) register_45 (.D(R_A), .C(C_dt), .en(multiplexer_44_out[2]), .Q(register_45_q));
  Register #(.Bits(32)) register_46 (.D(R_B), .C(C_dt), .en(multiplexer_44_out[2]), .Q(register_46_q));
  Register #(.Bits(16)) register_47 (
    .D({byte_D2_ex, byte_D3_ex}), .C(C_dt), .en(multiplexer_44_out[2]), .Q(register_47_q));
  Register register_48 (.D(CT_FU__EPOCH), .C(C_ct), .en(multiplexer_44_out[2]), .Q(register_48_q));
  Register #(.Bits(4)) register_49 (.D(CT_FU__INST), .C(C_ct), .en(multiplexer_44_out[2]), .Q(register_49_q));
  Register #(.Bits(2)) register_50 (
    .D({CT_FU__WR[1], and_52_out[0]}), .C(C_ct), .en(multiplexer_44_out[2]), .Q(register_50_q));
  assign CT_BUS__DAM = and_48_out[0] ? 1'b1 : 1'bz;  // Driver driver_29
  assign CT_BUS__DAR = and_48_out[0] ? 1'b1 : 1'bz;  // Driver driver_30
  assign {CT_RF__RB, CT_RF__MB} = and_48_out[1] ? byte_D1_ex : 8'bz;  // Driver driver_31
  assign CT_BUS__DDR = and_48_out[1] ? 1'b1 : 1'bz;  // Driver driver_32
  Driver driver_33 (.in(1'b1), .en(and_48_out[2]));  // open: out
  assign CT_BUS__DASDN = and_48_out[2] ? {and_47_out, byte_D1_ex[1]} : 3'bz;  // Driver driver_34
  Register #(.Bits(3)) register_51 (.D(and_48_out), .C(C_ct), .en(st_e__bf), .Q(register_51_q));
  assign CT_BUS__DAG = register_51_q[0] ? 1'b1 : 1'bz;  // Driver driver_35
  assign CT_RF__SCSE = register_51_q[0] ? 1'b1 : 1'bz;  // Driver driver_36
  assign CT_RF__SCAS = register_51_q[0] ? 1'b1 : 1'bz;  // Driver driver_37
  assign D_ST = register_51_q[1] ? 1'b1 : 1'bz;  // Driver driver_38
  assign CT_RF__SCN = register_51_q[1] ? register_16_q : 3'bz;  // Driver driver_39
  assign CT_BUS__DDG = register_51_q[1] ? 1'b1 : 1'bz;  // Driver driver_40
  assign D_LD = register_51_q[2] ? 1'b1 : 1'bz;  // Driver driver_41
  assign CT_RF__SCD = register_51_q[2] ? 1'b1 : 1'bz;  // Driver driver_42
  assign CT_RF__SCN = register_51_q[2] ? register_16_q : 3'bz;  // Driver driver_43
  assign CT_RF__DM = register_51_q[2] ? 1'b1 : 1'bz;  // Driver driver_44
  assign {CT_RF__WS, CT_RF__WM} = register_51_q[2] ? byte_D1_st : 8'bz;  // Driver driver_45
  assign CT_RF__E = register_51_q[2] ? 1'b1 : 1'bz;  // Driver driver_46
  assign st = register_51_q[0] ? 1'b1 : 1'bz;  // Driver driver_47
  assign D_MD = and_43_out[0] ? {byte_D1_ex[1], and_49_out[0]} : 2'bz;  // Driver driver_48
  assign {CT_RF__RA, CT_RF__MA} = and_43_out[0] ? {byte_D0[4:0], 3'b000} : 8'bz;  // Driver driver_49
  assign CT_ALU__CT = and_43_out[0] ? 9'h19 : 9'bz;  // Driver driver_50
  assign CT_ALU__M_old = and_43_out[0] ? 2'b11 : 2'bz;  // Driver driver_51
  assign CT_BUS__DAR = and_43_out[0] ? 1'b1 : 1'bz;  // Driver driver_52
  assign {CT_RF__RB, CT_RF__MB} = and_43_out[1] ? byte_D1_ex : 8'bz;  // Driver driver_53
  assign CT_BUS__DDR = and_43_out[1] ? 1'b1 : 1'bz;  // Driver driver_54
  Driver driver_55 (.in(1'b1), .en(and_43_out[2]));  // open: out
  Register #(.Bits(3)) register_52 (.D(and_43_out), .C(C_ct), .en(st_e__bf), .Q(register_52_q));
  assign CT_BUS__DAG = register_52_q[0] ? 1'b1 : 1'bz;  // Driver driver_56
  assign D_ST = register_52_q[1] ? 1'b1 : 1'bz;  // Driver driver_57
  assign CT_BUS__DDG = register_52_q[1] ? 1'b1 : 1'bz;  // Driver driver_58
  assign D_LD = register_52_q[2] ? 1'b1 : 1'bz;  // Driver driver_59
  assign CT_RF__DM = register_52_q[2] ? 1'b1 : 1'bz;  // Driver driver_60
  assign {CT_RF__WS, CT_RF__WM} = register_52_q[2] ? byte_D1_st : 8'bz;  // Driver driver_61
  assign CT_RF__E = register_52_q[2] ? 1'b1 : 1'bz;  // Driver driver_62
  assign st = register_52_q[0] ? 1'b1 : 1'bz;  // Driver driver_63
  assign CT_DEP__EA = and_50_out ? 1'b1 : 1'bz;  // Driver driver_64
  assign {CT_DEP__URA, CT_DEP__UMA} = and_50_out ? byte_D1 : 8'bz;  // Driver driver_65
  assign CT_DEP__EB = and_50_out ? not_18_out : 1'bz;  // Driver driver_66
  assign {CT_DEP__URB, CT_DEP__UMB} = and_50_out ? 8'hf8 : 8'bz;  // Driver driver_67
  Register register_53 (.D(multiplexer_14_out), .C(C_ct), .en(ex_e__bf), .Q(register_53_q));
  assign ex_nop = multiplexer_54_out ? 1'b1 : 1'bz;  // Driver driver_68
  assign CT_BUS__IDM = multiplexer_54_out ? 1'b1 : 1'bz;  // Driver driver_69
  assign CT_ALU__CT = multiplexer_54_out ? 9'h19 : 9'bz;  // Driver driver_70
  assign CT_ALU__M_old = multiplexer_54_out ? 2'b11 : 2'bz;  // Driver driver_71
  assign {CT_RF__RA, CT_RF__MA} = multiplexer_54_out ? byte_D1_ex : 8'bz;  // Driver driver_72
  Register register_54 (.D(multiplexer_54_out), .C(C_ct), .en(st_e__bf), .Q(register_54_q));
  assign CT_RF__PCSE = register_54_q ? 1'b1 : 1'bz;  // Driver driver_73
  assign CT_RF__PCJ = register_54_q ? 1'b1 : 1'bz;  // Driver driver_74
  assign CT_BUS__IDM = register_54_q ? 1'b1 : 1'bz;  // Driver driver_75
  assign st = register_54_q ? 1'b1 : 1'bz;  // Driver driver_76
  Register register_55 (.D(register_54_q), .C(C_ct), .en(cm_e__bf), .Q(register_55_q));
  assign CT_BUS__IDM = register_55_q ? 1'b1 : 1'bz;  // Driver driver_77
  Multiplexer #(.Bits(3)) multiplexer_29 (
    .sel(and_45_out), .in_0(CT_SC__O1), .in_1(CT_SC__O2), .out(multiplexer_29_out));
  Register register_56 (.D(and_55_out), .C(C_ct), .en(or_23_out), .Q(register_56_q[1]));
  or or_26 (register_19_q[0], ALU_busy, register_56_q[1], register_19_q[2]);
  assign and_58_out = nand_2_out & register_19_q;  // And and_58, 3 bits wide
  Multiplexer #(.Bits(4)) multiplexer_30 (
    .sel(register_19_q[1]), .in_0(CT_FU__INST), .in_1(register_29_q), .out(multiplexer_30_out));
  inst_comp inst_comp_2 (
    .A_id(register_29_q), .A_ep(register_30_q), .B_id(clr_id), .B_ep(clr_ep), .A_old(inst_comp_2_a_old));
  Multiplexer multiplexer_31 (
    .sel(register_19_q[1]), .in_0(CT_FU__EPOCH), .in_1(register_30_q), .out(multiplexer_31_out));
  Multiplexer multiplexer_32 (
    .sel(register_19_q[1]), .in_0(CT_ALU__WD), .in_1(register_31_q), .out(multiplexer_32_out));
  Multiplexer multiplexer_33 (
    .sel(register_19_q[1]), .in_0(CT_ALU__WF), .in_1(register_32_q), .out(multiplexer_33_out));
  Multiplexer #(.Bits(32)) multiplexer_34 (
    .sel(register_19_q[1]), .in_0(R_A), .in_1(register_33_q), .out(multiplexer_34_out));
  Multiplexer #(.Bits(32)) multiplexer_35 (
    .sel(register_19_q[1]), .in_0(multiplexer_12_out), .in_1(register_34_q), .out(multiplexer_35_out));
  Multiplexer #(.Bits(8)) multiplexer_36 (
    .sel(register_19_q[1]), .in_0(FL[7:0]), .in_1(register_35_q), .out(multiplexer_36_out));
  Multiplexer #(.Bits(9)) multiplexer_37 (
    .sel(register_19_q[1]), .in_0(CT_ALU__CT), .in_1(register_36_q), .out(multiplexer_37_out));
  Multiplexer #(.Bits(8)) multiplexer_38 (
    .sel(register_19_q[1]), .in_0(CT_FU__WR), .in_1(register_37_q), .out(multiplexer_38_out));
  Register register_57 (.D(and_56_out), .C(C_ct), .en(or_25_out), .Q(register_57_q[2]));
  Multiplexer #(.Bits(3)) multiplexer_39 (
    .sel(or_27_out), .in_0(not_15_out), .in_1(and_62_out), .out(multiplexer_39_out));
  or or_27 (or_27_out, and_62_out[0], and_62_out[1], and_62_out[2]);
  Multiplexer #(.Bits(4)) multiplexer_40 (
    .sel(register_57_q[2]), .in_0(CT_FU__INST), .in_1(register_38_q), .out(multiplexer_40_out));
  inst_comp inst_comp_3 (
    .A_id(register_38_q), .A_ep(register_39_q), .B_id(clr_id), .B_ep(clr_ep), .A_old(inst_comp_3_a_old));
  Multiplexer multiplexer_41 (
    .sel(register_57_q[2]), .in_0(CT_FU__EPOCH), .in_1(register_39_q), .out(multiplexer_41_out));
  Multiplexer #(.Bits(32)) multiplexer_42 (
    .sel(register_57_q[2]), .in_0(multiplexer_27_out), .in_1(register_40_q), .out(multiplexer_42_out));
  Multiplexer #(.Bits(8)) multiplexer_43 (
    .sel(register_57_q[2]), .in_0(CT_FU__WR), .in_1(register_41_q), .out(multiplexer_43_out));
  Register register_58 (.D(and_57_out), .C(C_ct), .en(or_28_out), .Q(register_58_q[2]));
  or or_28 (or_28_out, not_21_out, multiplexer_44_out[2]);
  Multiplexer #(.Bits(3)) multiplexer_44 (
    .sel(or_29_out), .in_0(not_17_out), .in_1(and_63_out), .out(multiplexer_44_out));
  or or_29 (or_29_out, and_63_out[0], and_63_out[1], and_63_out[2]);
  Multiplexer #(.Bits(4)) multiplexer_45 (
    .sel(register_58_q[2]), .in_0(CT_FU__INST), .in_1(register_42_q), .out(multiplexer_45_out));
  inst_comp inst_comp_4 (
    .A_id(register_42_q), .A_ep(register_43_q), .B_id(clr_id), .B_ep(clr_ep), .A_old(inst_comp_4_a_old));
  Multiplexer multiplexer_46 (
    .sel(register_58_q[2]), .in_0(CT_FU__EPOCH), .in_1(register_43_q), .out(multiplexer_46_out));
  Multiplexer multiplexer_47 (.sel(register_58_q[2]), .in_0(CT_MB__ST), .in_1(register_44_q), .out(multiplexer_47_out));
  Multiplexer #(.Bits(32)) multiplexer_48 (
    .sel(register_58_q[2]), .in_0(R_A), .in_1(register_45_q), .out(multiplexer_48_out));
  Multiplexer #(.Bits(32)) multiplexer_49 (
    .sel(register_58_q[2]), .in_0(R_B), .in_1(register_46_q), .out(multiplexer_49_out));
  Multiplexer #(.Bits(16)) multiplexer_50 (
    .sel(register_58_q[2]), .in_0({byte_D2_ex, byte_D3_ex}), .in_1(register_47_q), .out(multiplexer_50_out));
  Multiplexer multiplexer_51 (
    .sel(register_58_q[2]), .in_0(CT_FU__EPOCH), .in_1(register_48_q), .out(multiplexer_51_out));
  Multiplexer #(.Bits(4)) multiplexer_52 (
    .sel(register_58_q[2]), .in_0(CT_FU__INST), .in_1(register_49_q), .out(multiplexer_52_out));
  Multiplexer #(.Bits(2)) multiplexer_53 (
    .sel(register_58_q[2]), .in_0({CT_FU__WR[1], and_52_out[0]}), .in_1(register_50_q),
    .out(multiplexer_53_out));
  Multiplexer multiplexer_54 (.sel(multiplexer_10_out), .in_0(1'b0), .in_1(register_53_q), .out(multiplexer_54_out));
  Multiplexer multiplexer_55 (.sel(and_45_out), .in_0(CT_SC__D1), .in_1(CT_SC__D2), .out(multiplexer_55_out));
  Multiplexer multiplexer_56 (
    .sel(and_58_out[0]), .in_0(nand_1_out[0]), .in_1(nand_1_out[1]), .out(multiplexer_56_out));
  Multiplexer multiplexer_57 (
    .sel(register_19_q[1]), .in_0(CT_ALU__LD), .in_1(register_56_q[1]), .out(multiplexer_57_out));
  and and_59 (and_59_out, multiplexer_56_out, multiplexer_57_out);
  nand nand_2 (nand_2_out[2], ALU_busy, register_56_q[1], register_19_q[2]);
  nand nand_3 (nand_1_out[1], inst_comp_2_a_old, clr);
  Register #(.Bits(4)) register_59 (.D(multiplexer_30_out), .C(C_ct), .en(ALU_A_LD), .Q(ALU_A_INST));
  Register register_60 (.D(multiplexer_31_out), .C(C_ct), .en(ALU_A_LD), .Q(register_60_q));
  Register #(.Bits(32)) register_61 (.D(multiplexer_34_out), .C(C_dt), .en(ALU_A_LD), .Q(ALU_A_A));
  Register #(.Bits(32)) register_62 (.D(multiplexer_35_out), .C(C_dt), .en(ALU_A_LD), .Q(ALU_A_B));
  Register #(.Bits(8)) register_63 (.D(multiplexer_36_out), .C(C_dt), .en(ALU_A_LD), .Q(ALU_A_FI));
  Register #(.Bits(9)) register_64 (.D(multiplexer_37_out), .C(C_ct), .en(ALU_A_LD), .Q(ALU_A_CT));
  Register #(.Bits(8)) register_65 (.D(multiplexer_38_out), .C(C_ct), .en(ALU_A_LD), .Q({ALU_A_WR, ALU_A_RM}));
  Multiplexer multiplexer_58 (
    .sel(and_62_out[1]), .in_0(nand_4_out[1]), .in_1(nand_4_out[2]), .out(multiplexer_58_out));
  Multiplexer multiplexer_59 (
    .sel(register_57_q[2]), .in_0(CT_DIR__LD), .in_1(register_57_q[2]), .out(multiplexer_59_out));
  and and_60 (and_60_out, multiplexer_58_out, multiplexer_59_out);
  not not_22 (not_22_out, multiplexer_58_out);
  or or_30 (or_30_out, not_22_out, multiplexer_39_out[1]);
  nand nand_4 (nand_4_out[2], inst_comp_3_a_old, clr);
  Register #(.Bits(4)) register_66 (.D(multiplexer_40_out), .C(C_ct), .en(multiplexer_39_out[1]), .Q(register_66_q));
  Register register_67 (.D(multiplexer_41_out), .C(C_ct), .en(multiplexer_39_out[1]), .Q(register_67_q));
  Register #(.Bits(32)) register_68 (.D(multiplexer_42_out), .C(C_dt), .en(multiplexer_39_out[1]), .Q(register_68_q));
  Register #(.Bits(8)) register_69 (.D(multiplexer_43_out), .C(C_ct), .en(multiplexer_39_out[1]), .Q(register_69_q));
  Multiplexer multiplexer_60 (
    .sel(and_63_out[1]), .in_0(nand_5_out[1]), .in_1(nand_5_out[2]), .out(multiplexer_60_out));
  Multiplexer multiplexer_61 (
    .sel(register_58_q[2]), .in_0(CT_MB__LD), .in_1(register_58_q[2]), .out(multiplexer_61_out));
  and and_61 (and_61_out, multiplexer_60_out, multiplexer_61_out);
  not not_23 (not_23_out, multiplexer_60_out);
  nand nand_5 (nand_5_out[2], inst_comp_4_a_old, clr);
  Register #(.Bits(4)) register_70 (.D(multiplexer_45_out), .C(C_ct), .en(multiplexer_44_out[1]), .Q(register_70_q));
  Register register_71 (.D(multiplexer_46_out), .C(C_ct), .en(multiplexer_44_out[1]), .Q(register_71_q));
  Register register_72 (.D(multiplexer_47_out), .C(C_ct), .en(multiplexer_44_out[1]), .Q(register_72_q));
  Register #(.Bits(32)) register_73 (.D(multiplexer_48_out), .C(C_dt), .en(multiplexer_44_out[1]), .Q(register_73_q));
  Register #(.Bits(32)) register_74 (.D(multiplexer_49_out), .C(C_dt), .en(multiplexer_44_out[1]), .Q(register_74_q));
  Register #(.Bits(16)) register_75 (.D(multiplexer_50_out), .C(C_dt), .en(multiplexer_44_out[1]), .Q(register_75_q));
  Register register_76 (.D(multiplexer_51_out), .C(C_ct), .en(multiplexer_44_out[1]), .Q(register_76_q));
  Register #(.Bits(4)) register_77 (.D(multiplexer_52_out), .C(C_ct), .en(multiplexer_44_out[1]), .Q(register_77_q));
  Register #(.Bits(2)) register_78 (.D(multiplexer_53_out), .C(C_ct), .en(multiplexer_44_out[1]), .Q(register_78_q));
  addsub_4c32 addsub_4c32_1 (.a(SCS), .b({1'b0, CT_RF__SCN}), .sub(CT_RF__SCD), .s(scs_i), .c(sc_ov));
  addsub_4c32 addsub_4c32_2 (.a(SCA), .b({1'b0, multiplexer_29_out}), .sub(multiplexer_55_out), .s(sca_i), .c(sc_ov));
  nand nand_6 (nand_2_out[1], ALU_busy, register_56_q[1]);
  Register register_79 (.D(and_60_out), .C(C_ct), .en(or_30_out), .Q(register_79_q[1]));
  or or_31 (DIR_LD, register_79_q[1], register_57_q[2]);
  assign and_62_out = nand_10_out & {register_57_q[2], DIR_LD, register_57_q[0]};  // And and_62, 3 bits wide
  Multiplexer #(.Bits(4)) multiplexer_62 (
    .sel(DIR_LD), .in_0(CT_FU__INST), .in_1(register_66_q), .out(multiplexer_62_out));
  inst_comp inst_comp_5 (
    .A_id(register_66_q), .A_ep(register_67_q), .B_id(clr_id), .B_ep(clr_ep), .A_old(inst_comp_5_a_old));
  Multiplexer multiplexer_63 (.sel(DIR_LD), .in_0(CT_FU__EPOCH), .in_1(register_67_q), .out(multiplexer_63_out));
  Multiplexer #(.Bits(32)) multiplexer_64 (
    .sel(DIR_LD), .in_0(multiplexer_27_out), .in_1(register_68_q), .out(multiplexer_64_out));
  Multiplexer #(.Bits(8)) multiplexer_65 (
    .sel(DIR_LD), .in_0(CT_FU__WR), .in_1(register_69_q), .out(multiplexer_65_out));
  Register register_80 (.D(and_61_out), .C(C_ct), .en(or_32_out), .Q(register_80_q[1]));
  or or_32 (or_32_out, not_23_out, multiplexer_44_out[1]);
  or or_33 (register_58_q[1], register_80_q[1], register_58_q[2]);
  assign and_63_out = nand_11_out & register_58_q;  // And and_63, 3 bits wide
  Multiplexer #(.Bits(4)) multiplexer_66 (
    .sel(register_58_q[1]), .in_0(CT_FU__INST), .in_1(register_70_q), .out(multiplexer_66_out));
  inst_comp inst_comp_6 (
    .A_id(register_70_q), .A_ep(register_71_q), .B_id(clr_id), .B_ep(clr_ep), .A_old(inst_comp_6_a_old));
  Multiplexer multiplexer_67 (
    .sel(register_58_q[1]), .in_0(CT_FU__EPOCH), .in_1(register_71_q), .out(multiplexer_67_out));
  Multiplexer multiplexer_68 (.sel(register_58_q[1]), .in_0(CT_MB__ST), .in_1(register_72_q), .out(multiplexer_68_out));
  Multiplexer #(.Bits(32)) multiplexer_69 (
    .sel(register_58_q[1]), .in_0(R_A), .in_1(register_73_q), .out(multiplexer_69_out));
  Multiplexer #(.Bits(32)) multiplexer_70 (
    .sel(register_58_q[1]), .in_0(R_B), .in_1(register_74_q), .out(multiplexer_70_out));
  Multiplexer #(.Bits(16)) multiplexer_71 (
    .sel(register_58_q[1]), .in_0({byte_D2_ex, byte_D3_ex}), .in_1(register_75_q), .out(multiplexer_71_out));
  Multiplexer multiplexer_72 (
    .sel(register_58_q[1]), .in_0(CT_FU__EPOCH), .in_1(register_76_q), .out(multiplexer_72_out));
  Multiplexer #(.Bits(4)) multiplexer_73 (
    .sel(register_58_q[1]), .in_0(CT_FU__INST), .in_1(register_77_q), .out(multiplexer_73_out));
  Multiplexer #(.Bits(2)) multiplexer_74 (
    .sel(register_58_q[1]), .in_0({CT_FU__WR[1], and_52_out[0]}), .in_1(register_78_q),
    .out(multiplexer_74_out));
  not not_24 (nand_2_out[0], ALU_busy);
  nand nand_7 (nand_1_out[0], or_36_out, clr);
  inst_comp inst_comp_7 (.A_id(ALU_A_INST), .A_ep(register_60_q), .B_id(clr_id), .B_ep(clr_ep), .A_old(ALU_A_CMP));
  Multiplexer multiplexer_75 (
    .sel(and_62_out[0]), .in_0(nand_4_out[0]), .in_1(nand_4_out[1]), .out(multiplexer_75_out));
  Multiplexer multiplexer_76 (.sel(DIR_LD), .in_0(CT_DIR__LD), .in_1(register_79_q[1]), .out(multiplexer_76_out));
  and and_64 (and_64_out, multiplexer_75_out, multiplexer_76_out);
  or or_34 (register_57_q[0], DIR_busy, register_79_q[1], register_57_q[2]);
  nand nand_8 (nand_4_out[1], inst_comp_5_a_old, clr);
  Register #(.Bits(4)) register_81 (.D(multiplexer_62_out), .C(C_ct), .en(DIR_LD), .Q(DIR_INST));
  Register register_82 (.D(multiplexer_63_out), .C(C_ct), .en(DIR_LD), .Q(register_82_q));
  Register #(.Bits(32)) register_83 (.D(multiplexer_64_out), .C(C_dt), .en(DIR_LD), .Q(DIR));
  Register #(.Bits(8)) register_84 (.D(multiplexer_65_out), .C(C_ct), .en(DIR_LD), .Q(DIR_WR));
  Multiplexer multiplexer_77 (
    .sel(and_63_out[0]), .in_0(nand_5_out[0]), .in_1(nand_5_out[1]), .out(multiplexer_77_out));
  Multiplexer multiplexer_78 (
    .sel(register_58_q[1]), .in_0(CT_MB__LD), .in_1(register_80_q[1]), .out(multiplexer_78_out));
  and and_65 (and_65_out, multiplexer_77_out, multiplexer_78_out);
  or or_35 (register_58_q[0], MB_busy, register_80_q[1], register_58_q[2]);
  nand nand_9 (nand_5_out[1], inst_comp_6_a_old, clr);
  Register #(.Bits(4)) register_85 (.D(multiplexer_66_out), .C(C_ct), .en(MB_LD), .Q(MB_INSt_t));
  Register register_86 (.D(multiplexer_67_out), .C(C_ct), .en(MB_LD), .Q(MB_ep));
  Register register_87 (.D(multiplexer_68_out), .C(C_ct), .en(MB_LD), .Q(MB_type__st));
  Register #(.Bits(32)) register_88 (.D(multiplexer_69_out), .C(C_dt), .en(MB_LD), .Q(MB_data));
  Register #(.Bits(32)) register_89 (.D(multiplexer_70_out), .C(C_dt), .en(MB_LD), .Q(register_89_q));
  Register #(.Bits(16)) register_90 (.D(multiplexer_71_out), .C(C_dt), .en(MB_LD), .Q(register_90_q));
  Register register_91 (.D(multiplexer_72_out), .C(C_ct), .en(MB_LD), .Q(MB_ep));
  Register #(.Bits(4)) register_92 (.D(multiplexer_73_out), .C(C_ct), .en(MB_LD), .Q(MB_INST));
  Register #(.Bits(2)) register_93 (.D(multiplexer_74_out), .C(C_ct), .en(MB_LD), .Q(MB_MD));
  Register #(.Bits(4)) register_94 (.D(multiplexer_30_out), .C(C_dt), .en(ALU_B_LD), .Q(ALU_B_INST));
  Register register_95 (.D(multiplexer_31_out), .C(C_dt), .en(ALU_B_LD), .Q(register_95_q));
  Register #(.Bits(32)) register_96 (.D(multiplexer_34_out), .C(C_dt), .en(ALU_B_LD), .Q(ALU_B_A));
  Register #(.Bits(32)) register_97 (.D(multiplexer_35_out), .C(C_dt), .en(ALU_B_LD), .Q(ALU_B_B));
  Register #(.Bits(8)) register_98 (.D(multiplexer_36_out), .C(C_dt), .en(ALU_B_LD), .Q(ALU_B_FI));
  Register #(.Bits(9)) register_99 (.D(multiplexer_37_out), .C(C_ct), .en(ALU_A_LD), .Q(ALU_B_CT));
  Register #(.Bits(8)) register_100 (.D(multiplexer_38_out), .C(C_ct), .en(ALU_B_LD), .Q({ALU_B_WR, ALU_B_RM}));
  nand nand_10 (nand_10_out[2], DIR_busy, register_79_q[1], register_57_q[2]);
  nand nand_11 (nand_11_out[2], MB_busy, register_80_q[1], register_58_q[2]);
  and and_66 (and_66_out[0], ALU_A_LD, multiplexer_32_out);
  and and_67 (and_66_out[1], ALU_A_LD, multiplexer_33_out);
  and and_68 (and_68_out[0], ALU_B_LD, multiplexer_32_out);
  and and_69 (and_68_out[1], ALU_B_LD, multiplexer_33_out);
  or or_36 (or_36_out, ALU_A_CMP, ALU_B_CMP);
  nand nand_12 (nand_10_out[1], DIR_busy, register_79_q[1]);
  not not_25 (nand_10_out[0], DIR_busy);
  inst_comp inst_comp_8 (
    .A_id(DIR_INST), .A_ep(register_82_q), .B_id(clr_id), .B_ep(clr_ep), .A_old(inst_comp_8_a_old));
  nand nand_13 (nand_11_out[1], MB_busy, register_80_q[1]);
  not not_26 (nand_11_out[0], MB_busy);
  inst_comp inst_comp_9 (.A_id(MB_INSt_t), .A_ep(MB_ep), .B_id(clr_id), .B_ep(clr_ep), .A_old(inst_comp_9_a_old));
  add_s16c32 add_s16c32_1 (.a(register_89_q), .b(register_90_q), .s(MB_addr));  // open: c
  and and_70 (and_70_out, ~and_66_out[0], ALU_A_STD);  // And
  and and_71 (and_71_out, ~and_66_out[1], ALU_A_STF);  // And
  and and_72 (and_72_out, ~and_68_out[0], ALU_A_STD);  // And
  and and_73 (and_73_out, ~and_68_out[1], ALU_A_STF);  // And
  inst_comp inst_comp_10 (.A_id(ALU_B_INST), .A_ep(register_95_q), .B_id(clr_id), .B_ep(clr_ep), .A_old(ALU_B_CMP));
  nand nand_14 (nand_4_out[0], inst_comp_8_a_old, clr);
  nand nand_15 (nand_5_out[0], inst_comp_9_a_old, clr);
  D_FF #(.Bits(2)) d_ff_1 (.D(and_66_out), .C(C_ct), .Q(d_ff_1_q));  // open: nQ
  RS_FF rs_ff_3 (.S(and_66_out[0]), .C(C_ct), .R(and_70_out), .nQ(rs_ff_3_nq));  // open: Q
  RS_FF rs_ff_4 (.S(and_66_out[1]), .C(C_ct), .R(and_71_out), .nQ(rs_ff_4_nq));  // open: Q
  D_FF #(.Bits(2)) d_ff_2 (.D(and_68_out), .C(C_ct), .Q(d_ff_2_q));  // open: nQ
  RS_FF rs_ff_5 (.S(and_68_out[0]), .C(C_ct), .R(and_72_out), .nQ(rs_ff_5_nq));  // open: Q
  RS_FF rs_ff_6 (.S(and_68_out[1]), .C(C_ct), .R(and_73_out), .nQ(rs_ff_6_nq));  // open: Q
  and and_74 (and_74_out, ~and_64_out, DIR_ST);  // And
  and and_75 (and_75_out, ~and_64_out, DIR_RD);  // And
  bus16_demux bus16_demux_1 (.bus(V_inst), .E(DIR_ST), .id(DIR_INST));
  and and_76 (DIR_CLR, clr, inst_comp_8_a_old);
  and and_77 (MB_st__e, and_65_out, MB_type__st);
  and and_78 (MB_ld__e, and_65_out, ~MB_type__st);  // And
  and and_79 (and_79_out, byte_I0[0], byte_I0_iv[1], byte_I0_iv[2], byte_I0_iv[3], byte_I0[4], byte_I0[5], byte_I0[6], byte_I0_iv[7]);
  D_FF #(.Bits(2)) d_ff_3 (.D(d_ff_1_q), .C(C_ct), .Q({d_ff_3_q[1], ALU_A_RE}));  // open: nQ
  D_FF #(.Bits(2)) d_ff_4 (.D(d_ff_2_q), .C(C_ct), .Q({d_ff_4_q[1], ALU_B_RE}));  // open: nQ
  // alu_32 alu_32_1: pin names not known; wires that end beside it: ALU_A_A, ALU_A_B, ALU_A_FI, ALU_A_CT, ALU_A_RM, alu_32_1_p6, alu_32_1_p6, alu_32_1_p8, alu_32_1_p9, alu_32_1_p9, alu_32_1_p11, alu_32_1_p12, alu_32_1_p12, alu_32_1_p14, ALU_A_R, ALU_A_F
  alu_32 alu_32_2 (
    .A(ALU_B_A), .B(ALU_B_B), .F_I(ALU_B_FI), .CT(ALU_B_CT), .RM(ALU_B_RM), .E_A(alu_32_1_p8),
    .E_B(alu_32_1_p11), .E(alu_32_1_p14), .R_O(ALU_B_R), .F_O(ALU_B_F));
  RS_FF rs_ff_7 (.S(and_64_out), .C(C_ct), .R(and_74_out), .nQ(rs_ff_7_nq));  // open: Q
  RS_FF rs_ff_8 (.S(and_64_out), .C(C_ct), .R(and_75_out), .Q(DIR_RD));  // open: nQ
  or or_37 (or_37_out, MEM_LD__RD, LDB_ldV);
  and and_80 (and_80_out, byte_I0_iv[0], byte_I0_iv[1], byte_I0_iv[2], byte_I0_iv[3], byte_I0[4], byte_I0[5], byte_I0[6], byte_I0_iv[7]);
  and and_81 (and_81_out, byte_I0[0], byte_I0[1], byte_I0_iv[2], byte_I0_iv[3], byte_I0[4], byte_I0[5], byte_I0[6], byte_I0_iv[7]);
  Multiplexer multiplexer_79 (.sel(ex_nop), .in_0(and_81_out), .in_1(1'b0));  // open: out
  and and_82 (and_82_out, com1, CT_FL__W1);
  and and_83 (and_83_out, com2, CT_FL__W2);
  and and_84 (and_84_out, ALU_B_STD, ~and_90_out);  // And
  and and_85 (and_85_out, ALU_B_STF, ~and_90_out);  // And
  and and_86 (and_86_out, ALU_A_STD, ~and_91_out);  // And
  and and_87 (and_87_out, ALU_A_STF, ~and_91_out);  // And
  PullDown #(.Bits(32)) pulldown_14 (.out(alu_32_1_p12));
  PullDown #(.Bits(32)) pulldown_15 (.out(alu_32_1_p14));
  or or_38 (DIR_free, DIR_ST, rs_ff_7_nq);
  Multiplexer #(.Bits(32)) multiplexer_80 (.sel(LDB_ldV), .in_0(MEM_LD__D), .in_1(LDB_ldD), .out(multiplexer_80_out));
  Multiplexer #(.Bits(4)) multiplexer_81 (.sel(LDB_ldV), .in_0(MEM_LD__INST), .in_1(LD_id), .out(multiplexer_81_out));
  Multiplexer multiplexer_82 (.sel(ex_nop), .in_0(and_80_out), .in_1(1'b0), .out(multiplexer_82_out));
  Multiplexer multiplexer_83 (.sel(ex_nop), .in_0(and_79_out), .in_1(1'b0), .out(multiplexer_83_out));
  or or_39 (CT_RF__FLS, and_82_out, and_83_out);
  RS_FF rs_ff_9 (.S(ALU_A_RE), .C(C_ct), .R(ALU_A_FRD), .Q(ALU_A_DRD));  // open: nQ
  RS_FF rs_ff_10 (.S(d_ff_3_q[1]), .C(C_ct), .R(ALU_A_FRD), .Q(ALU_A_FRD));  // open: nQ
  RS_FF rs_ff_11 (.S(ALU_B_RE), .C(C_ct), .R(ALU_B_DRD), .Q(ALU_B_DRD));  // open: nQ
  RS_FF rs_ff_12 (.S(d_ff_4_q[1]), .C(C_ct), .R(ALU_B_FRD), .Q(ALU_B_FRD));  // open: nQ
  RS_FF rs_ff_13 (.S(and_84_out), .C(C_ct), .R(and_90_out), .Q(rs_ff_13_q));  // open: nQ
  RS_FF rs_ff_14 (.S(and_85_out), .C(C_ct), .R(and_90_out), .Q(rs_ff_14_q));  // open: nQ
  RS_FF rs_ff_15 (.S(and_86_out), .C(C_ct), .R(and_91_out), .Q(rs_ff_15_q));  // open: nQ
  RS_FF rs_ff_16 (.S(and_87_out), .C(C_ct), .R(and_91_out), .Q(rs_ff_16_q));  // open: nQ
  and and_88 (and_88_out, and_65_out, MB_free);
  assign CT_DEP__EA = and_80_out ? 1'b1 : 1'bz;  // Driver driver_78
  assign {CT_DEP__URA, CT_DEP__UMA} = and_80_out ? byte_I1 : 8'bz;  // Driver driver_79
  Register register_101 (.D(multiplexer_82_out), .C(C_ct), .en(ex_e__bf), .Q(register_101_q));
  assign ex_nop = register_101_q ? 1'b1 : 1'bz;  // Driver driver_80
  assign CT_BUS__IDM = register_101_q ? 1'b1 : 1'bz;  // Driver driver_81
  assign {CT_RF__RA, CT_RF__MA} = register_101_q ? byte_D1_ex : 8'bz;  // Driver driver_82
  assign CT_ALU__CT = register_101_q ? 9'h19 : 9'bz;  // Driver driver_83
  assign CT_ALU__M_old = register_101_q ? 2'b11 : 2'bz;  // Driver driver_84
  assign {CT_RF__RB, CT_RF__MB} = register_101_q ? 8'he8 : 8'bz;  // Driver driver_85
  assign CT_BUS__DAM = register_101_q ? 1'b1 : 1'bz;  // Driver driver_86
  assign CT_BUS__DAR = register_101_q ? 1'b1 : 1'bz;  // Driver driver_87
  assign CT_BUS__DDR = register_101_q ? 1'b1 : 1'bz;  // Driver driver_88
  Register register_102 (.D(register_101_q), .C(C_ct), .en(st_e__bf), .Q(register_102_q));
  assign CT_BUS__IDM = register_102_q ? 1'b1 : 1'bz;  // Driver driver_89
  assign CT_RF__SCSE = register_102_q ? 1'b1 : 1'bz;  // Driver driver_90
  assign CT_RF__SCAS = register_102_q ? 1'b1 : 1'bz;  // Driver driver_91
  assign CT_RF__SCN = register_102_q ? 3'b100 : 3'bz;  // Driver driver_92
  assign CT_RF__PCSE = register_102_q ? 1'b1 : 1'bz;  // Driver driver_93
  assign CT_RF__PCJ = register_102_q ? 1'b1 : 1'bz;  // Driver driver_94
  assign CT_BUS__DAG = register_102_q ? 1'b1 : 1'bz;  // Driver driver_95
  assign CT_BUS__DDG = register_102_q ? 1'b1 : 1'bz;  // Driver driver_96
  assign D_ST = register_102_q ? 1'b1 : 1'bz;  // Driver driver_97
  assign st = register_102_q ? 1'b1 : 1'bz;  // Driver driver_98
  Register register_103 (.D(register_102_q), .C(C_ct), .en(cm_e__bf), .Q(register_103_q));
  assign CT_BUS__IDM = register_103_q ? 1'b1 : 1'bz;  // Driver driver_99
  Register register_104 (.D(multiplexer_83_out), .C(C_ct), .en(ex_e__bf), .Q(register_104_q));
  assign ex_nop = register_104_q ? 1'b1 : 1'bz;  // Driver driver_100
  assign CT_BUS__IDM = register_104_q ? 1'b1 : 1'bz;  // Driver driver_101
  assign CT_BUS__DAM = register_104_q ? 1'b1 : 1'bz;  // Driver driver_102
  assign CT_BUS__DAR = register_104_q ? 1'b1 : 1'bz;  // Driver driver_103
  assign CT_BUS__DASDN = register_104_q ? 3'b100 : 3'bz;  // Driver driver_104
  Register register_105 (.D(register_104_q), .C(C_ct), .en(st_e__bf), .Q(register_105_q));
  assign CT_BUS__IDM = register_105_q ? 1'b1 : 1'bz;  // Driver driver_105
  assign D_LD = register_105_q ? 1'b1 : 1'bz;  // Driver driver_106
  assign CT_RF__SCSE = register_105_q ? 1'b1 : 1'bz;  // Driver driver_107
  assign CT_RF__SCD = register_105_q ? 1'b1 : 1'bz;  // Driver driver_108
  assign CT_RF__SCN = register_105_q ? 3'b100 : 3'bz;  // Driver driver_109
  assign CT_RF__SCAS = register_105_q ? 1'b1 : 1'bz;  // Driver driver_110
  assign CT_RF__PCSE = register_105_q ? 1'b1 : 1'bz;  // Driver driver_111
  assign CT_RF__PCJ = register_105_q ? 1'b1 : 1'bz;  // Driver driver_112
  assign CT_RF__PCR = register_105_q ? 1'b1 : 1'bz;  // Driver driver_113
  assign CT_BUS__DAG = register_105_q ? 1'b1 : 1'bz;  // Driver driver_114
  assign st = register_105_q ? 1'b1 : 1'bz;  // Driver driver_115
  Register register_106 (.D(register_105_q), .C(C_ct), .en(cm_e__bf), .Q(register_106_q));
  assign CT_BUS__IDM = register_106_q ? 1'b1 : 1'bz;  // Driver driver_116
  Register register_107 (.D(1'b0), .C(C_ct), .en(ex_e__bf), .Q(register_107_q));
  assign ex_nop = register_107_q ? 1'b1 : 1'bz;  // Driver driver_117
  assign hlt = register_107_q ? 1'b1 : 1'bz;  // Driver driver_118
  assign CT_BUS__IDM = register_107_q ? 1'b1 : 1'bz;  // Driver driver_119
  assign CT_BUS__IDM = register_107_q ? 1'b1 : 1'bz;  // Driver driver_120
  Register register_108 (.D(register_107_q), .C(C_ct), .en(st_e__bf), .Q(register_108_q));
  assign CT_RF__PCH = register_108_q ? 1'b1 : 1'bz;  // Driver driver_121
  assign CT_RF__PCSE = register_108_q ? 1'b1 : 1'bz;  // Driver driver_122
  assign CT_BUS__IDM = register_108_q ? 1'b1 : 1'bz;  // Driver driver_123
  assign st = register_108_q ? 1'b1 : 1'bz;  // Driver driver_124
  or or_40 (or_40_out, ALU_B_STD, rs_ff_13_q);
  or or_41 (or_41_out, ALU_B_STF, rs_ff_14_q);
  or or_42 (or_42_out, ALU_A_STD, rs_ff_15_q);
  or or_43 (or_43_out, ALU_A_STF, rs_ff_16_q);
  and and_89 (DIR_LD, and_64_out, DIR_free);
  not not_27 (DIR_busy, DIR_free);
  Multiplexer multiplexer_84 (.sel(MB_type__st), .in_0(LDB_busy), .in_1(STB_busy), .out(MB_busy));
  DipSwitch dipswitch_3 (.out(dipswitch_3_out));
  DipSwitch dipswitch_4 (.out(dipswitch_4_out));
  DipSwitch dipswitch_5 (.out(dipswitch_5_out));
  or or_44 (or_44_out, ALU_A_STD, rs_ff_3_nq);
  or or_45 (or_45_out, ALU_A_STF, rs_ff_4_nq);
  or or_46 (or_46_out, ALU_B_STD, rs_ff_5_nq);
  or or_47 (or_47_out, ALU_B_STF, rs_ff_6_nq);
  and and_90 (and_90_out, or_40_out, or_41_out);
  bus16_demux bus16_demux_2 (.bus(V_inst), .E(and_90_out), .id(ALU_B_INST));
  and and_91 (and_91_out, or_42_out, or_43_out);
  bus16_demux bus16_demux_3 (.bus(V_inst), .E(and_91_out), .id(ALU_A_INST));
  nor nor_4 (ALU_busy, ALU_A_LRD, ALU_B_LRD);
  or or_48 (ALU_free, ALU_A_LRD, ALU_B_LRD);
  Register #(.Bits(32)) register_109 (.D(ALU_A_R), .C(C_dt), .en(ALU_A_RE), .Q(ALU_A_T__R));
  Register #(.Bits(8)) register_110 (.D(ALU_A_F), .C(C_dt), .en(ALU_A_RE), .Q(ALU_A_T__F));
  Register #(.Bits(32)) register_111 (.D(ALU_B_R), .C(C_dt), .en(ALU_B_RE), .Q(ALU_B_T__R));
  Register #(.Bits(8)) register_112 (.D(ALU_B_F), .C(C_dt), .en(ALU_B_RE), .Q(ALU_B_T__F));
  bus16_demux bus16_demux_4 (.bus(V_inst), .E(and_88_out), .id(MB_INST));
  not not_28 (MB_free, MB_busy);
  store_buffer store_buffer_1 (
    .C(C_dt), .LD(dipswitch_3_out), .W_d(MB_st__e), .inst_W(MB_INST), .D(MB_data), .A(MB_addr), .MD(MB_MD),
    .W_id(CT_ISS__OSTB), .epoch(epoch_IS), .inst(inst_IS), .com1(com1), .com2(com2), .com1_id(com1_inst),
    .com2_id(com2_inst), .ld_ep(MB_ep), .ld_id(MB_INST), .ld_addr(MB_addr), .full(STB_busy), .V(STB_M__V),
    .D_O(STB_M__D), .A_O(STB_M__A), .MD_O(STB_M__MD), .id_O(STB_M__ID), .ep_O(STB_M__EP), .ld_V(LDB_ldV),
    .ld_D(LDB_ldD));
  load_buffer load_buffer_1 (
    .C(C_dt), .LD(dipswitch_4_out), .LDB(dipswitch_5_out), .W_d(or_37_out), .inst_WD(multiplexer_81_out),
    .D(multiplexer_80_out), .W_a(MB_ld__e), .inst_WA(MB_INST), .A(MB_addr), .MD(MB_MD), .W_id(CT_ISS__OLDB),
    .epoch(epoch_IS), .inst(inst_IS), .com1(com1), .com2(com2), .com1_id(com1_inst), .com2_id(com2_inst),
    .st(MB_st__e), .st_ep(MB_ep), .st_id(MB_INST), .st_addr(MB_addr), .st_data(MB_data), .full(LDB_busy),
    .V(load_buffer_1_v), .D_O(load_buffer_1_d_o), .id_O(load_buffer_1_id_o), .M_V(LDB_M__V), .M_A(LDB_M__A),
    .M_MD(LDB_M__MD), .M_id(LDB_M__ID), .M_ep(LDB_M__EP), .fl(load_buffer_1_fl), .fl_ep(load_buffer_1_fl_ep),
    .fl_id(load_buffer_1_fl_id));
  not not_29 (not_29_out, STB_busy);
  not not_30 (not_30_out, LDB_busy);
  Multiplexer #(.Bits(8)) multiplexer_85 (.sel(and_83_out), .in_0(CT_FL__D1), .in_1(CT_FL__D2), .out(fl_i));
  and and_92 (ALU_A_LD, and_59_out, or_45_out, or_44_out);
  and and_93 (ALU_A_LRD, or_44_out, or_45_out);
  nand nand_16 (nand_16_out, or_44_out, or_45_out);
  and and_94 (ALU_B_LD, nand_16_out, and_59_out, or_47_out, or_46_out);
  and and_95 (ALU_B_LRD, or_46_out, or_47_out);
  and and_96 (MB_LD, CT_STB__LD, not_29_out);
  and and_97 (LDB_LD, CT_STB__LD, not_30_out);
  and and_98 (ALU_A_CLR, clr, ALU_A_CMP);
  and and_99 (ALU_B_CLR, clr, ALU_B_CMP);
  and and_100 (and_100_out, byte_I0[3], byte_I0[0]);
  and and_101 (and_101_out, byte_I0[2], byte_I0[0]);
  and and_102 (and_102_out, byte_I0_iv[3], byte_I0_iv[2], byte_I0[1], byte_I0_iv[0]);
  and and_103 (and_103_out, byte_I0_iv[2], byte_I0_iv[0]);
  and and_104 (and_104_out, byte_I0[2], byte_I0[0]);
  and and_105 (and_105_out, byte_I0[1], byte_I0[2], byte_I0[4]);
  and and_106 (and_106_out, byte_I0[3], byte_I0[4]);
  and and_107 (and_107_out, byte_I0[4], byte_I0[3], byte_I0_iv[1], byte_I0_iv[2], byte_I0_iv[5], byte_I0_iv[6], byte_I0_iv[7]);
  or or_49 (or_49_out, and_100_out, and_101_out, and_102_out);
  or or_50 (or_50_out, byte_I0[3], byte_I0[1], and_103_out, and_104_out);
  nor nor_5 (nor_5_out, and_105_out, and_106_out);
  and and_108 (and_108_out, byte_I0_iv[7], byte_I0_iv[6], byte_I0[5]);
  and and_109 (and_109_out, byte_I0_iv[7], byte_I0[6], byte_I0_iv[5]);
  store_controller store_controller_1 (
    .C(C_ct), .in1(ALU_A_DRD), .in2(ALU_B_DRD), .in3(DIR_RD), .in4(1'b0), .in5(1'b0), .in6(1'b0), .in7(1'b0),
    .in8(1'b0), .clr({{5{1'b0}}, DIR_CLR, ALU_A_CLR, ALU_B_CLR}), .D1_sel(store_controller_1_d1_sel),
    .D2_sel(store_controller_1_d2_sel), .ST1(CT_ROB__GEN__STA), .ST2(CT_ROB__GEN__STB), .out1(ALU_A_STD),
    .out2(ALU_B_STD), .out6(DIR_ST));  // open: out3, out4, out5, out7, out8
  store_controller store_controller_2 (
    .C(C_ct), .in1(ALU_B_FRD), .in2(ALU_A_FRD), .in3(1'b0), .in4(1'b0), .in5(1'b0), .in6(1'b0), .in7(1'b0),
    .in8(1'b0), .clr({{5{1'b0}}, DIR_CLR, ALU_A_CLR, ALU_B_CLR}), .D1_sel(store_controller_2_d1_sel),
    .D2_sel(store_controller_2_d2_sel), .ST1(CT_ROB__FL__STA), .ST2(CT_ROB__FL__STB), .out1(ALU_A_STF),
    .out2(ALU_B_STF));  // open: out3, out4, out5, out6, out7, out8
  and and_110 (and_110_out, byte_I0_iv[0], byte_I0_iv[1], byte_I0[2], byte_I0[3], byte_I0[4], byte_I0_iv[5], byte_I0_iv[6], byte_I0_iv[7]);
  and and_111 (and_111_out, byte_I0[1], byte_I0_iv[2], byte_I0[3], byte_I0[4], byte_I0_iv[5], byte_I0_iv[6], byte_I0_iv[7]);
  and and_112 (and_112_out, byte_I0[1], byte_I0[2], byte_I0[3], byte_I0[4], byte_I0_iv[5], byte_I0_iv[6], byte_I0_iv[7]);
  or or_51 (or_51_out, and_108_out, and_109_out);
  and and_113 (and_113_out, byte_I0_iv[7], byte_I0_iv[6], byte_I0_iv[5], byte_I0_iv[4]);
  and and_114 (and_114_out, byte_I0_iv[7], byte_I0_iv[6], byte_I0_iv[5], byte_I0[4], byte_I0_iv[3]);
  or or_52 (or_52_out, and_110_out, and_111_out);
  not not_31 (not_31_out, byte_I0[0]);
  not not_32 (not_32_out, or_49_out);
  and and_115 (and_115_out, and_112_out, byte_I0[0]);
  and and_116 (and_116_out, not_31_out, and_112_out);
  or or_53 (or_53_out, and_113_out, and_107_out, and_114_out);
  assign issue = or_53_out ? dp_e : 1'bz;  // Driver driver_125
  assign CT_ISS__URA = or_53_out ? 1'b1 : 1'bz;  // Driver driver_126
  assign CT_ISS__URB = or_53_out ? not_32_out : 1'bz;  // Driver driver_127
  assign CT_ISS__RA = or_53_out ? byte_I1[7:3] : 5'bz;  // Driver driver_128
  assign CT_ISS__RB = or_53_out ? byte_I2[7:3] : 5'bz;  // Driver driver_129
  assign CT_ISS__UFL = or_53_out ? or_50_out : 1'bz;  // Driver driver_130
  assign CT_ISS__ORC = or_53_out ? nor_5_out : 1'bz;  // Driver driver_131
  assign CT_ISS__RC = or_53_out ? byte_I1[7:3] : 5'bz;  // Driver driver_132
  assign CT_ISS__OFL = or_53_out ? 1'b1 : 1'bz;  // Driver driver_133
  assign CT_ISS__UFU = or_53_out ? 3'b001 : 3'bz;  // Driver driver_134
  assign CT_ISS__URA = and_110_out ? 1'b1 : 1'bz;  // Driver driver_135
  assign CT_ISS__RA = and_110_out ? byte_I2[7:3] : 5'bz;  // Driver driver_136
  assign issue = or_52_out ? dp_e : 1'bz;  // Driver driver_137
  assign CT_ISS__ORC = or_52_out ? 1'b1 : 1'bz;  // Driver driver_138
  assign CT_ISS__RC = or_52_out ? byte_I1[7:3] : 5'bz;  // Driver driver_139
  assign CT_ISS__UFU = or_52_out ? 3'b010 : 3'bz;  // Driver driver_140
  assign issue = and_112_out ? dp_e : 1'bz;  // Driver driver_141
  assign CT_ISS__USC = and_112_out ? 1'b1 : 1'bz;  // Driver driver_142
  assign CT_ISS__OSC = and_112_out ? 1'b1 : 1'bz;  // Driver driver_143
  assign CT_ISS__URA = and_115_out ? 1'b1 : 1'bz;  // Driver driver_144
  assign CT_ISS__RA = and_115_out ? byte_I1[7:3] : 5'bz;  // Driver driver_145
  assign CT_ISS__UFU = and_115_out ? 3'b011 : 3'bz;  // Driver driver_146
  assign CT_ISS__ORC = and_116_out ? 1'b1 : 1'bz;  // Driver driver_147
  assign CT_ISS__RC = and_116_out ? byte_I1[7:3] : 5'bz;  // Driver driver_148
  assign CT_ISS__UFU = and_116_out ? 3'b100 : 3'bz;  // Driver driver_149
  assign issue = or_51_out ? dp_e : 1'bz;  // Driver driver_150
  assign CT_ISS__URA = or_51_out ? 1'b1 : 1'bz;  // Driver driver_151
  assign CT_ISS__RA = or_51_out ? byte_I0[4:0] : 5'bz;  // Driver driver_152
  assign CT_ISS__URB = and_109_out ? 1'b1 : 1'bz;  // Driver driver_153
  assign CT_ISS__RB = and_109_out ? byte_I1[7:3] : 5'bz;  // Driver driver_154
  assign CT_ISS__UFU = and_109_out ? 3'b011 : 3'bz;  // Driver driver_155
  assign CT_ISS__ORC = and_108_out ? 1'b1 : 1'bz;  // Driver driver_156
  assign CT_ISS__RC = and_108_out ? byte_I1[7:3] : 5'bz;  // Driver driver_157
  assign CT_ISS__UFU = and_108_out ? 3'b100 : 3'bz;  // Driver driver_158
  // data_select_32 data_select_32_1: pin names not known; wires that end beside it: store_controller_1_d1_sel, store_controller_1_d2_sel, ALU_A_T__R, ALU_B_T__R, DIR, {32{1'b0}}, {32{1'b0}}, {32{1'b0}}, {32{1'b0}}, {32{1'b0}}, ROB_GEN_DA, ROB_GEN_DB
  data_select_8 data_select_8_1 (
    .D1_sel(store_controller_2_d1_sel), .D2_sel(store_controller_2_d2_sel), .in1(ALU_A_T__F),
    .in2(ALU_B_T__F), .in3({8{1'b0}}), .in4({8{1'b0}}), .in5({8{1'b0}}), .in6({8{1'b0}}), .in7({8{1'b0}}),
    .in8({8{1'b0}}), .out1(ROB_FL_A), .out2(ROB_FL_B));
  and and_117 (and_117_out, byte_I0_iv[4], byte_I0[5], byte_I0[6], byte_I0_iv[7]);
  data_select_8 data_select_8_2 (
    .D1_sel(store_controller_1_d1_sel), .D2_sel(store_controller_1_d2_sel), .in1({ALU_A_WR, ALU_A_RM}),
    .in2({ALU_B_WR, ALU_B_RM}), .in3(DIR_WR), .in4({8{1'b0}}), .in5({8{1'b0}}), .in6({8{1'b0}}),
    .in7({8{1'b0}}), .in8({8{1'b0}}), .out1(ROB_GEN_WA), .out2(ROB_GEN_WB));
  data_select_4 data_select_4_1 (
    .D1_sel(store_controller_2_d1_sel), .D2_sel(store_controller_2_d2_sel), .in1(ALU_A_INST),
    .in2(ALU_B_INST), .in3(4'b0000), .in4(4'b0000), .in5(4'b0000), .in6(4'b0000), .in7(4'b0000),
    .in8(4'b0000), .out1(ROB_FL_INSTA), .out2(ROB_FL_INSTB));
  Comparator #(.Bits(3)) comparator_4 (.a(byte_I0[2:0]), .b(3'b110), .eq(comparator_4_eq));  // open: gt, lt
  not not_33 (not_33_out, comparator_4_eq);
  and and_118 (and_118_out, byte_I0_iv[0], byte_I0_iv[1], byte_I0_iv[2], byte_I0_iv[3], byte_I0[4], byte_I0[5], byte_I0[6], byte_I0_iv[7]);
  and and_119 (and_119_out, byte_I0[0], byte_I0_iv[1], byte_I0_iv[2], byte_I0_iv[3], byte_I0[4], byte_I0[5], byte_I0[6], byte_I0_iv[7]);
  and and_120 (and_120_out, byte_I0[0], byte_I0[1], byte_I0_iv[2], byte_I0_iv[3], byte_I0[4], byte_I0[5], byte_I0[6], byte_I0_iv[7]);
  assign issue = and_117_out ? dp_e : 1'bz;  // Driver driver_159
  assign CT_ISS__URA = and_117_out ? 1'b1 : 1'bz;  // Driver driver_160
  assign CT_ISS__RA = and_117_out ? byte_I1[7:3] : 5'bz;  // Driver driver_161
  assign CT_ISS__UFL = and_117_out ? not_33_out : 1'bz;  // Driver driver_162
  assign issue = and_118_out ? dp_e : 1'bz;  // Driver driver_163
  assign CT_ISS__URA = and_118_out ? 1'b1 : 1'bz;  // Driver driver_164
  assign CT_ISS__RA = and_118_out ? byte_I1[7:3] : 5'bz;  // Driver driver_165
  assign CT_ISS__USC = and_118_out ? 1'b1 : 1'bz;  // Driver driver_166
  assign CT_ISS__OSC = and_118_out ? 1'b1 : 1'bz;  // Driver driver_167
  assign issue = and_119_out ? dp_e : 1'bz;  // Driver driver_168
  assign CT_ISS__USC = and_119_out ? 1'b1 : 1'bz;  // Driver driver_169
  assign CT_ISS__OSC = and_119_out ? 1'b1 : 1'bz;  // Driver driver_170
  assign issue = and_120_out ? dp_e : 1'bz;  // Driver driver_171
  data_select_4 data_select_4_2 (
    .D1_sel(store_controller_1_d1_sel), .D2_sel(store_controller_1_d2_sel), .in1(ALU_A_INST),
    .in2(ALU_B_INST), .in3(DIR_INST), .in4(4'b0000), .in5(4'b0000), .in6(4'b0000), .in7(4'b0000),
    .in8(4'b0000), .out1(ROB_GEN_INSTA), .out2(ROB_GEN_INSTB));
  D_FF #(.Bits(8)) d_ff_5 (.D({4'b0000, MB_free, DIR_free, ALU_free, 1'b1}), .C(C_ct), .Q(FU_free));  // open: nQ
  // res_station res_station_1: pin names not known; wires that end beside it: C_ct, res_station_1_p2, issue, {byte_I0, byte_I1, byte_I2, byte_I3}, epoch_IS, inst_IS, CT_ISS__URA, CT_ISS__URB, CT_ISS__RA, CT_ISS__RB, CT_ISS__USC, CT_ISS__UFL, CT_ISS__UFU, CT_ISS__ORC, CT_ISS__RC, CT_ISS__OSC, CT_ISS__OFL, com1, com2, com1_inst, com2_inst, CT_RF__R1[7:3], CT_RF__R2[7:3], CT_SC__W1, CT_SC__W2, CT_FL__W1, CT_FL__W2, clr, clr_ep, clr_id, CT_DISP, {res_station_1_p32, byte_D1, byte_D2, byte_D3}, epoch_DP, inst_DP
  not not_34 (res_station_1_p2, E);
  PullDown #(.Bits(3)) pulldown_16 (.out(CT_ISS__UFU));
  PullDown pulldown_17 (.out(CT_ISS__OSTB));
  Multiplexer #(.Bits(8)) multiplexer_86 (.sel(CT_DISP), .in_0(8'h72), .in_1(res_station_1_p32), .out(byte_D0));
  PullDown pulldown_18 (.out(clr));
  PullDown pulldown_19 (.out(clr_ep));
  PullDown #(.Bits(4)) pulldown_20 (.out(clr_id));
  PullDown pulldown_21 (.out(CT_ALU__M));
  PullDown pulldown_22 (.out(CT_ALU__LD));
  PullDown pulldown_23 (.out(CT_ALU__WD));
  PullDown pulldown_24 (.out(CT_ALU__WF));
  PullDown pulldown_25 (.out(CT_FU__EPOCH));
  PullDown #(.Bits(4)) pulldown_26 (.out(CT_FU__INST));
  PullDown #(.Bits(8)) pulldown_27 (.out(CT_FU__WR));
  PullDown pulldown_28 (.out(CT_DIR__LD));
  PullDown pulldown_29 (.out(CT_DIR__M));
  PullDown pulldown_30 (.out(CT_DIR__MS));
  PullDown pulldown_31 (.out(MB_ep));
  PullDown #(.Bits(4)) pulldown_32 (.out(LD_id));
  PullDown #(.Bits(32)) pulldown_33 (.out(LD_addr));
  PullDown pulldown_34 (.out(CT_STB__LD));
  PullDown pulldown_35 (.out(CT_LDB__LD));
  PullDown pulldown_36 (.out(CT_MB__LD));
  PullDown pulldown_37 (.out(CT_MB__ST));
  PullDown pulldown_38 (.out(CT_ISS__OLDB));
  PullDown pulldown_39 (.out(kernel_inst));
  PullDown pulldown_40 (.out(CT_RF__E));
  PullDown pulldown_41 (.out(CT_RF__DM));
  PullDown #(.Bits(5)) pulldown_42 (.out(CT_RF__WS));
  PullDown #(.Bits(3)) pulldown_43 (.out(CT_RF__WM));
  PullDown #(.Bits(5)) pulldown_44 (.out(CT_RF__RA));
  PullDown #(.Bits(3)) pulldown_45 (.out(CT_RF__MA));
  PullDown #(.Bits(5)) pulldown_46 (.out(CT_RF__RB));
  PullDown #(.Bits(3)) pulldown_47 (.out(CT_RF__MB));
  PullDown pulldown_48 (.out(CT_RF__PCSE));
  PullDown pulldown_49 (.out(CT_RF__PCJ));
  PullDown pulldown_50 (.out(CT_RF__PCR));
  PullDown #(.Bits(3)) pulldown_51 (.out(CT_RF__SCN));
  PullDown pulldown_52 (.out(CT_RF__SCD));
  PullDown pulldown_53 (.out(CT_RF__SCAS));
  PullDown pulldown_54 (.out(CT_RF__SCSE));
  PullDown pulldown_55 (.out(CT_RF__FLS));
  PullDown #(.Bits(4)) pulldown_56 (.out(4'b0001));
  PullDown #(.Bits(9)) pulldown_57 (.out(CT_ALU__CT));
  PullDown pulldown_58 (.out(CT_ALU__M));
  PullDown pulldown_59 (.out(CT_ALU__M2));
  PullDown pulldown_60 (.out(CT_BUS__IAR));
  PullDown pulldown_61 (.out(CT_BUS__IAG));
  PullDown pulldown_62 (.out(CT_BUS__IDR));
  PullDown pulldown_63 (.out(CT_BUS__IDM));
  PullDown pulldown_64 (.out(CT_BUS__DAR));
  PullDown pulldown_65 (.out(CT_BUS__DAM));
  PullDown pulldown_66 (.out(CT_BUS__DAG));
  PullDown pulldown_67 (.out(CT_BUS__DDR));
  PullDown pulldown_68 (.out(CT_BUS__DDG));
  PullDown pulldown_69 (.out(I_LD));
  PullDown pulldown_70 (.out(D_LD));
  PullDown pulldown_71 (.out(D_ST));
  PullDown #(.Bits(2)) pulldown_72 (.out(D_MD));
  PullDown pulldown_73 (.out(CT_MVR));
  PullDown pulldown_74 (.out(issue));
  PullDown pulldown_75 (.out(CT_ISS__URA));
  PullDown pulldown_76 (.out(CT_ISS__URB));
  PullDown #(.Bits(5)) pulldown_77 (.out(CT_ISS__RA));
  PullDown #(.Bits(5)) pulldown_78 (.out(CT_ISS__RB));
  PullDown pulldown_79 (.out(CT_ISS__USC));
  PullDown pulldown_80 (.out(CT_ISS__UFL));
  PullDown pulldown_81 (.out(CT_ISS__ORC));
  PullDown #(.Bits(5)) pulldown_82 (.out(CT_ISS__RC));
  PullDown pulldown_83 (.out(CT_ISS__OSC));
  PullDown pulldown_84 (.out(CT_ISS__OFL));
  PullDown pulldown_85 (.out(CT_ROB__EX__E));
  PullDown pulldown_86 (.out(CT_ROB__ST__E));
  PullDown #(.Bits(3)) pulldown_87 (.out(CT_BUS__DASDN));
  PullDown pulldown_88 (.out(CT_BUS__DDM));
  PullDown pulldown_89 (.out(CT_RF__PCH));
  PullDown pulldown_90 (.out(hlt));
  PullDown pulldown_91 (.out(ex_nop));

  assign CLK_str = 1'b0;
  assign CSH_mode = 2'b00;
  assign CSH_run = 1'b0;
  assign DMA_sel = 3'b000;
  assign DMA_str = 1'b0;
  assign INT_out = 1'b0;
  assign INT_str = 1'b0;
  assign MMU_sel = 2'b00;
  assign MMU_str = 1'b0;

  // Other names for the same wires on the sheet: disp_32[31:0] = {byte_D0, byte_D1, byte_D2, byte_D3};
  //   FU_CLR[2:0] = {DIR_CLR, ALU_A_CLR, ALU_B_CLR}; ALU_A_WR[2:0] = ALU_A_RM; ALU_B_WR[2:0] = ALU_B_RM;
  //   ALU_R[31:0] = ALU_A_T__R; ALU_T__R[31:0] = ALU_A_T__R; imm16_2_ex[15:0] = {byte_D2_ex, byte_D3_ex}; C_i = C_dt;
  //   ext_e = cm_e; ext_e__bf = cm_e__bf; int_proc = FL[14]; trap = FL[15];
  //   issue_32[31:0] = {byte_I0, byte_I1, byte_I2, byte_I3}; issue_e = dp_e; MEM_AC = D_valid; st_e = rf_e

  // Notes on the sheet:
  //   C: Hz: 4
  //   bus_e: default 1
  //   D_MD: 0:32
  //   1:16
  //   2:8
  //   3:u.u
  //   I_valid: default 1
  //   D_valid: default 1
  //   kernal mode system
  //   interrupt system
  //   pipeline controller
  //   inst id manager
  //   tests
  //   IO pins
  //   primeary signals
  //   decode circuit
  //   ALU
  //   register
  //   register system
  //   ROB
  //   program counter controller
  //   bus system
  //   data bus ctrl
  //   stack
  //   RAM
  //   jump
  //   stack circuit
  //   ALU system
  //   dir circuit
  //   load/store circuit
  //   call
  //   return
  //   halt
  //   flag circuit
  //   issue circuit
  //   FU aribiter
  //   control bus
endmodule
